// Logisim project TP1a5_sen2.circ as structural Verilog: 35 circuits, main circuit decodeur_4to7
module decodeur_4to7 (
  input  i0,
  input  i1,
  input  i2,
  input  i3,
  output a,
  output b,
  output c,
  output d,
  output e,
  output f,
  output g
);

  wire and_1_out, and_2_out, and_3_out, and_4_out, and_5_out, and_6_out, and_7_out, and_8_out, and_9_out,
       and_10_out, and_11_out, and_12_out, and_13_out, and_14_out, and_15_out, and_16_out, and_17_out,
       and_18_out, and_19_out, and_20_out, and_21_out, and_22_out, and_23_out, and_24_out, and_25_out,
       and_26_out, and_27_out, and_28_out, and_29_out, and_30_out, and_31_out, and_32_out, and_33_out,
       and_34_out, and_35_out, and_36_out, not_1_out, not_2_out, not_3_out, not_4_out, not_5_out, not_6_out,
       not_7_out, not_8_out, not_9_out, not_10_out, not_11_out, not_12_out, not_13_out, not_14_out,
       not_15_out, not_16_out, not_17_out, not_18_out, not_19_out, not_20_out, not_21_out, not_22_out,
       not_23_out, not_24_out, not_25_out, not_26_out, not_27_out, not_28_out, not_29_out, not_30_out,
       not_31_out, not_32_out, not_33_out, not_34_out, not_35_out, not_36_out, not_37_out, not_38_out,
       not_39_out, not_40_out, not_41_out, not_42_out, not_43_out, not_44_out, not_45_out;

  not not_1 (not_1_out, i2);
  and and_1 (and_1_out, not_1_out, not_2_out);
  not not_2 (not_2_out, i0);
  and and_2 (and_2_out, i2, i1);
  not not_3 (not_3_out, i3);
  and and_3 (and_3_out, not_3_out, i1);
  and and_4 (and_4_out, i3, not_4_out);
  not not_4 (not_4_out, i0);
  not not_5 (not_5_out, i3);
  and and_5 (and_5_out, not_5_out, i2, i0);
  and and_6 (and_6_out, i3, not_6_out, not_7_out);
  not not_6 (not_6_out, i2);
  not not_7 (not_7_out, i1);
  not not_8 (not_8_out, i3);
  and and_7 (and_7_out, not_8_out, not_9_out);
  not not_9 (not_9_out, i2);
  not not_10 (not_10_out, i2);
  and and_8 (and_8_out, not_10_out, not_11_out);
  not not_11 (not_11_out, i1);
  not not_12 (not_12_out, i2);
  and and_9 (and_9_out, not_12_out, not_13_out);
  not not_13 (not_13_out, i0);
  not not_14 (not_14_out, i3);
  and and_10 (and_10_out, not_14_out, not_15_out, not_16_out);
  not not_15 (not_15_out, i1);
  not not_16 (not_16_out, i0);
  not not_17 (not_17_out, i3);
  and and_11 (and_11_out, not_17_out, i1, i0);
  and and_12 (and_12_out, i3, not_18_out, i0);
  not not_18 (not_18_out, i1);
  not not_19 (not_19_out, i3);
  and and_13 (and_13_out, not_19_out, not_20_out);
  not not_20 (not_20_out, i1);
  and and_14 (and_14_out, i3, not_21_out);
  not not_21 (not_21_out, i2);
  not not_22 (not_22_out, i3);
  and and_15 (and_15_out, not_22_out, i0);
  not not_23 (not_23_out, i1);
  and and_16 (and_16_out, not_23_out, i0);
  not not_24 (not_24_out, i3);
  and and_17 (and_17_out, not_24_out, i2);
  and and_18 (and_18_out, i3, not_25_out);
  not not_25 (not_25_out, i1);
  not not_26 (not_26_out, i3);
  and and_19 (and_19_out, not_26_out, not_27_out, not_28_out);
  not not_27 (not_27_out, i2);
  not not_28 (not_28_out, i0);
  not not_29 (not_29_out, i2);
  and and_20 (and_20_out, not_29_out, i1, i0);
  and and_21 (and_21_out, i2, i1, not_30_out);
  not not_30 (not_30_out, i0);
  and and_22 (and_22_out, i2, not_31_out, i0);
  not not_31 (not_31_out, i1);
  not not_32 (not_32_out, i2);
  and and_23 (and_23_out, not_32_out, not_33_out);
  not not_33 (not_33_out, i0);
  and and_24 (and_24_out, i3, i2);
  and and_25 (and_25_out, i1, not_34_out);
  not not_34 (not_34_out, i0);
  and and_26 (and_26_out, i3, i1);
  not not_35 (not_35_out, i1);
  and and_27 (and_27_out, not_35_out, not_36_out);
  not not_36 (not_36_out, i0);
  and and_28 (and_28_out, i3, i1);
  and and_29 (and_29_out, i2, not_37_out);
  not not_37 (not_37_out, i0);
  and and_30 (and_30_out, i3, not_38_out);
  not not_38 (not_38_out, i2);
  not not_39 (not_39_out, i3);
  and and_31 (and_31_out, not_39_out, i2, not_40_out);
  not not_40 (not_40_out, i1);
  not not_41 (not_41_out, i2);
  and and_32 (and_32_out, not_41_out, i1);
  and and_33 (and_33_out, i1, not_42_out);
  not not_42 (not_42_out, i0);
  and and_34 (and_34_out, i3, i0);
  and and_35 (and_35_out, i3, not_43_out);
  not not_43 (not_43_out, i2);
  not not_44 (not_44_out, i3);
  and and_36 (and_36_out, not_44_out, i2, not_45_out);
  not not_45 (not_45_out, i1);
  or or_1 (a, and_1_out, and_2_out, and_3_out, and_4_out, and_5_out, and_6_out);
  or or_2 (b, and_7_out, and_8_out, and_9_out, and_10_out, and_11_out, and_12_out);
  or or_3 (c, and_13_out, and_14_out, and_15_out, and_16_out, and_17_out);
  or or_4 (d, and_18_out, and_19_out, and_20_out, and_21_out, and_22_out);
  or or_5 (e, and_23_out, and_24_out, and_25_out, and_26_out);
  or or_6 (f, and_27_out, and_28_out, and_29_out, and_30_out, and_31_out);
  or or_7 (g, and_32_out, and_33_out, and_34_out, and_35_out, and_36_out);
endmodule

module test_decodeur_4to7 (
);

  wire decodeur_4to7_1_a, decodeur_4to7_1_b, decodeur_4to7_1_c, decodeur_4to7_1_d, decodeur_4to7_1_e,
       decodeur_4to7_1_f, decodeur_4to7_1_g, decodeur_4to7_2_a, decodeur_4to7_2_b, decodeur_4to7_2_c,
       decodeur_4to7_2_d, decodeur_4to7_2_e, decodeur_4to7_2_f, decodeur_4to7_2_g, In_all_2_sw1,
       In_all_2_sw2, In_all_2_sw3, In_all_2_sw4, In_all_sw1, In_all_sw2, In_all_sw3, In_all_sw4;

  DipSwitch #(.number(4)) In_all (.sw1(In_all_sw1), .sw2(In_all_sw2), .sw3(In_all_sw3), .sw4(In_all_sw4));
  decodeur_4to7 decodeur_4to7_1 (
    .i0(In_all_sw4), .i1(In_all_sw3), .i2(In_all_sw2), .i3(In_all_sw1), .a(decodeur_4to7_1_a),
    .b(decodeur_4to7_1_b), .c(decodeur_4to7_1_c), .d(decodeur_4to7_1_d), .e(decodeur_4to7_1_e),
    .f(decodeur_4to7_1_f), .g(decodeur_4to7_1_g));
  _7_Segment_Display Out_all (
    .g(decodeur_4to7_1_g), .f(decodeur_4to7_1_f), .a(decodeur_4to7_1_a), .b(decodeur_4to7_1_b),
    .e(decodeur_4to7_1_e), .d(decodeur_4to7_1_d), .c(decodeur_4to7_1_c));  // open: dp
  DipSwitch #(.number(4)) In_all_2 (.sw1(In_all_2_sw1), .sw2(In_all_2_sw2), .sw3(In_all_2_sw3), .sw4(In_all_2_sw4));
  decodeur_4to7 decodeur_4to7_2 (
    .i0(In_all_2_sw4), .i1(In_all_2_sw3), .i2(In_all_2_sw2), .i3(In_all_2_sw1), .a(decodeur_4to7_2_a),
    .b(decodeur_4to7_2_b), .c(decodeur_4to7_2_c), .d(decodeur_4to7_2_d), .e(decodeur_4to7_2_e),
    .f(decodeur_4to7_2_f), .g(decodeur_4to7_2_g));
  _7_Segment_Display Out_all_2 (
    .g(decodeur_4to7_2_g), .f(decodeur_4to7_2_f), .a(decodeur_4to7_2_a), .b(decodeur_4to7_2_b),
    .e(decodeur_4to7_2_e), .d(decodeur_4to7_2_d), .c(decodeur_4to7_2_c));  // open: dp
endmodule

module add3 (
  input  i3,
  input  i2,
  input  i1,
  input  i0,
  output s3,
  output s2,
  output s1,
  output s0
);

  wire and_1_out, and_2_out, and_3_out, and_4_out, and_5_out, and_6_out, and_7_out, and_8_out, and_9_out,
       and_10_out;

  and and_1 (and_1_out, ~i3, ~i2, i0);  // AND_Gate
  and and_2 (and_2_out, i3, ~i0);  // AND_Gate
  and and_3 (and_3_out, i2, i1, ~i0);  // AND_Gate
  and and_4 (and_4_out, i1, i0);
  or or_1 (s1, and_4_out, and_5_out, and_6_out);
  and and_5 (and_5_out, i3, ~i0);  // AND_Gate
  and and_6 (and_6_out, ~i2, i1);  // AND_Gate
  and and_7 (and_7_out, ~i1, ~i0, i2);  // AND_Gate
  or or_2 (s2, and_7_out, and_8_out);
  and and_8 (and_8_out, i3, i0);
  and and_9 (and_9_out, i0, i2);
  or or_3 (s3, and_9_out, and_10_out, i3);
  and and_10 (and_10_out, i2, i1);
  or or_4 (s0, and_1_out, and_2_out, and_3_out);
endmodule

module test_add3 (
  output s3,
  output s2,
  output s1,
  output s0
);

  wire input_all_sw1, input_all_sw2, input_all_sw3, input_all_sw4;

  DipSwitch #(.number(4)) input_all (
    .sw1(input_all_sw1), .sw2(input_all_sw2), .sw3(input_all_sw3), .sw4(input_all_sw4));
  add3 add3test (
    .i3(input_all_sw4), .i2(input_all_sw3), .i1(input_all_sw2), .i0(input_all_sw1), .s3(s3), .s2(s2),
    .s1(s1), .s0(s0));
endmodule

module test_codeur_BNtoBCD (
);

  wire BNtoBCD_s0, BNtoBCD_s1, BNtoBCD_s2, BNtoBCD_s3, BNtoBCD_s4, BNtoBCD_s5, BNtoBCD_s6, BNtoBCD_s7,
       BNtoBCD_s8, BNtoBCD_s9, BNtoBCD_s10, BNtoBCD_s11, BNtoBCD_s12, BNtoBCD_s13, BNtoBCD_s14, BNtoBCD_s15,
       decodeur_4t07_1_a, decodeur_4t07_1_b, decodeur_4t07_1_c, decodeur_4t07_1_d, decodeur_4t07_1_e,
       decodeur_4t07_1_f, decodeur_4t07_1_g, decodeur_4t07_2_a, decodeur_4t07_2_b, decodeur_4t07_2_c,
       decodeur_4t07_2_d, decodeur_4t07_2_e, decodeur_4t07_2_f, decodeur_4t07_2_g, decodeur_4t07_3_a,
       decodeur_4t07_3_b, decodeur_4t07_3_c, decodeur_4t07_3_d, decodeur_4t07_3_e, decodeur_4t07_3_f,
       decodeur_4t07_3_g, decodeur_4t07_4_a, decodeur_4t07_4_b, decodeur_4t07_4_c, decodeur_4t07_4_d,
       decodeur_4t07_4_e, decodeur_4t07_4_f, decodeur_4t07_4_g, input_all_sw1, input_all_sw2, input_all_sw3,
       input_all_sw4, input_all_sw5, input_all_sw6, input_all_sw7, input_all_sw8, input_all_sw9,
       input_all_sw10;

  DipSwitch #(.number(10)) input_all (
    .sw1(input_all_sw1), .sw2(input_all_sw2), .sw3(input_all_sw3), .sw4(input_all_sw4), .sw5(input_all_sw5),
    .sw6(input_all_sw6), .sw7(input_all_sw7), .sw8(input_all_sw8), .sw9(input_all_sw9), .sw10(input_all_sw10));
  codeur_BNtoBCD BNtoBCD (
    .i7(input_all_sw3), .i8(input_all_sw2), .i9(input_all_sw1), .i6(input_all_sw4), .i5(input_all_sw5),
    .i4(input_all_sw6), .i3(input_all_sw7), .i2(input_all_sw8), .i1(input_all_sw9), .i0(input_all_sw10),
    .s0(BNtoBCD_s0), .s1(BNtoBCD_s1), .s5(BNtoBCD_s5), .s9(BNtoBCD_s9), .s13(BNtoBCD_s13), .s2(BNtoBCD_s2),
    .s6(BNtoBCD_s6), .s10(BNtoBCD_s10), .s14(BNtoBCD_s14), .s3(BNtoBCD_s3), .s7(BNtoBCD_s7),
    .s11(BNtoBCD_s11), .s15(BNtoBCD_s15), .s4(BNtoBCD_s4), .s8(BNtoBCD_s8), .s12(BNtoBCD_s12));
  _7_Segment_Display a0 (
    .g(decodeur_4t07_1_g), .f(decodeur_4t07_1_f), .a(decodeur_4t07_1_a), .b(decodeur_4t07_1_b),
    .e(decodeur_4t07_1_e), .d(decodeur_4t07_1_d), .c(decodeur_4t07_1_c));  // open: dp
  decodeur_4to7 decodeur_4t07_1 (
    .i0(BNtoBCD_s0), .i1(BNtoBCD_s1), .i2(BNtoBCD_s2), .i3(BNtoBCD_s3), .a(decodeur_4t07_1_a),
    .b(decodeur_4t07_1_b), .c(decodeur_4t07_1_c), .d(decodeur_4t07_1_d), .e(decodeur_4t07_1_e),
    .f(decodeur_4t07_1_f), .g(decodeur_4t07_1_g));
  _7_Segment_Display a1 (
    .g(decodeur_4t07_2_g), .f(decodeur_4t07_2_f), .a(decodeur_4t07_2_a), .b(decodeur_4t07_2_b),
    .e(decodeur_4t07_2_e), .d(decodeur_4t07_2_d), .c(decodeur_4t07_2_c));  // open: dp
  decodeur_4to7 decodeur_4t07_2 (
    .i0(BNtoBCD_s4), .i1(BNtoBCD_s5), .i2(BNtoBCD_s6), .i3(BNtoBCD_s7), .a(decodeur_4t07_2_a),
    .b(decodeur_4t07_2_b), .c(decodeur_4t07_2_c), .d(decodeur_4t07_2_d), .e(decodeur_4t07_2_e),
    .f(decodeur_4t07_2_f), .g(decodeur_4t07_2_g));
  _7_Segment_Display a2 (
    .g(decodeur_4t07_3_g), .f(decodeur_4t07_3_f), .a(decodeur_4t07_3_a), .b(decodeur_4t07_3_b),
    .e(decodeur_4t07_3_e), .d(decodeur_4t07_3_d), .c(decodeur_4t07_3_c));  // open: dp
  decodeur_4to7 decodeur_4t07_3 (
    .i0(BNtoBCD_s8), .i1(BNtoBCD_s9), .i2(BNtoBCD_s10), .i3(BNtoBCD_s11), .a(decodeur_4t07_3_a),
    .b(decodeur_4t07_3_b), .c(decodeur_4t07_3_c), .d(decodeur_4t07_3_d), .e(decodeur_4t07_3_e),
    .f(decodeur_4t07_3_f), .g(decodeur_4t07_3_g));
  _7_Segment_Display a3 (
    .g(decodeur_4t07_4_g), .f(decodeur_4t07_4_f), .a(decodeur_4t07_4_a), .b(decodeur_4t07_4_b),
    .e(decodeur_4t07_4_e), .d(decodeur_4t07_4_d), .c(decodeur_4t07_4_c));  // open: dp
  decodeur_4to7 decodeur_4t07_4 (
    .i0(BNtoBCD_s12), .i1(BNtoBCD_s13), .i2(BNtoBCD_s14), .i3(BNtoBCD_s15), .a(decodeur_4t07_4_a),
    .b(decodeur_4t07_4_b), .c(decodeur_4t07_4_c), .d(decodeur_4t07_4_d), .e(decodeur_4t07_4_e),
    .f(decodeur_4t07_4_f), .g(decodeur_4t07_4_g));
endmodule

module codeur_BNtoBCD (
  input  i7,
  input  i8,
  input  i9,
  input  i6,
  input  i5,
  input  i4,
  input  i3,
  input  i2,
  input  i1,
  input  i0,
  output s0,
  output s1,
  output s5,
  output s9,
  output s13,
  output s2,
  output s6,
  output s10,
  output s14,
  output s3,
  output s7,
  output s11,
  output s15,
  output s4,
  output s8,
  output s12
);

  wire add3_1_s0, add3_1_s1, add3_1_s2, add3_1_s3, add3_2_s0, add3_2_s1, add3_2_s2, add3_2_s3, add3_3_s0,
       add3_3_s1, add3_3_s2, add3_3_s3, add3_4_s0, add3_4_s1, add3_4_s2, add3_4_s3, add3_5_s0, add3_5_s1,
       add3_5_s2, add3_5_s3, add3_6_s0, add3_6_s1, add3_6_s2, add3_6_s3, add3_7_s0, add3_7_s1, add3_7_s2,
       add3_7_s3, add3_8_s0, add3_8_s1, add3_8_s2, add3_8_s3, add3_9_s0, add3_9_s1, add3_9_s2, add3_9_s3;

  add3 add3_8 (
    .i3(add3_6_s2), .i2(add3_6_s1), .i1(add3_6_s0), .i0(i2), .s3(add3_8_s3), .s2(add3_8_s2), .s1(add3_8_s1),
    .s0(add3_8_s0));
  add3 add3_10 (.i3(add3_8_s2), .i2(add3_8_s1), .i1(add3_8_s0), .i0(i1), .s3(s4), .s2(s3), .s1(s2), .s0(s1));
  add3 add3_2 (
    .i3(add3_1_s2), .i2(add3_1_s1), .i1(add3_1_s0), .i0(i6), .s3(add3_2_s3), .s2(add3_2_s2), .s1(add3_2_s1),
    .s0(add3_2_s0));
  add3 add3_3 (
    .i3(add3_2_s2), .i2(add3_2_s1), .i1(add3_2_s0), .i0(i5), .s3(add3_3_s3), .s2(add3_3_s2), .s1(add3_3_s1),
    .s0(add3_3_s0));
  add3 add3_4 (
    .i3(add3_3_s2), .i2(add3_3_s1), .i1(add3_3_s0), .i0(i4), .s3(add3_4_s3), .s2(add3_4_s2), .s1(add3_4_s1),
    .s0(add3_4_s0));
  add3 add3_6 (
    .i3(add3_4_s2), .i2(add3_4_s1), .i1(add3_4_s0), .i0(i3), .s3(add3_6_s3), .s2(add3_6_s2), .s1(add3_6_s1),
    .s0(add3_6_s0));
  add3 add3_11 (.i3(add3_9_s2), .i2(add3_9_s1), .i1(add3_9_s0), .i0(add3_8_s3), .s3(s8), .s2(s7), .s1(s6), .s0(s5));
  add3 add3_1 (.i3(1'b0), .i2(i9), .i1(i8), .i0(i7), .s3(add3_1_s3), .s2(add3_1_s2), .s1(add3_1_s1), .s0(add3_1_s0));
  add3 add3_5 (
    .i3(1'b0), .i2(add3_1_s3), .i1(add3_2_s3), .i0(add3_3_s3), .s3(add3_5_s3), .s2(add3_5_s2),
    .s1(add3_5_s1), .s0(add3_5_s0));
  add3 add3_7 (
    .i3(add3_5_s2), .i2(add3_5_s1), .i1(add3_5_s0), .i0(add3_4_s3), .s3(add3_7_s3), .s2(add3_7_s2),
    .s1(add3_7_s1), .s0(add3_7_s0));
  add3 add3_9 (
    .i3(add3_7_s2), .i2(add3_7_s1), .i1(add3_7_s0), .i0(add3_6_s3), .s3(add3_9_s3), .s2(add3_9_s2),
    .s1(add3_9_s1), .s0(add3_9_s0));
  add3 add3_12 (.i3(1'b0), .i2(add3_5_s3), .i1(add3_7_s3), .i0(add3_9_s3), .s3(s12), .s2(s11), .s1(s10), .s0(s9));

  assign s0 = i0;
  assign s13 = 1'b0;
  assign s14 = 1'b0;
  assign s15 = 1'b0;
endmodule

module add1 (
  input  A,
  input  B,
  input  Ri,
  output S,
  output Ro
);

  wire and_1_out, and_2_out, and_3_out, and_4_out, and_5_out, and_6_out, and_7_out, not_1_out, not_2_out,
       not_3_out, not_4_out, not_5_out, not_6_out;

  not not_1 (not_1_out, A);
  not not_2 (not_2_out, B);
  not not_3 (not_3_out, A);
  not not_4 (not_4_out, Ri);
  not not_5 (not_5_out, B);
  not not_6 (not_6_out, Ri);
  and and_1 (and_1_out, B, Ri);
  and and_2 (and_2_out, A, Ri);
  and and_3 (and_3_out, A, B);
  and and_4 (and_4_out, not_1_out, not_2_out, Ri);
  and and_5 (and_5_out, not_3_out, B, not_4_out);
  and and_6 (and_6_out, A, not_5_out, not_6_out);
  and and_7 (and_7_out, A, B, Ri);
  or or_1 (Ro, and_1_out, and_2_out, and_3_out);
  or or_2 (S, and_4_out, and_5_out, and_6_out, and_7_out);
endmodule

module add4b (
  input  Cin,
  input  [3:0] A,
  input  [3:0] B,
  output [3:0] S,
  output Cout
);

  wire add1_1_ro, add1_2_ro, add1_3_ro;

  add1 add1_1 (.A(A[0]), .B(B[0]), .Ri(Cin), .S(S[0]), .Ro(add1_1_ro));
  add1 add1_2 (.A(A[1]), .B(B[1]), .Ri(add1_1_ro), .S(S[1]), .Ro(add1_2_ro));
  add1 add1_3 (.A(A[2]), .B(B[2]), .Ri(add1_2_ro), .S(S[2]), .Ro(add1_3_ro));
  add1 add1_4 (.A(A[3]), .B(B[3]), .Ri(add1_3_ro), .S(S[3]), .Ro(Cout));
endmodule

module test_add4b (
);

  wire codeur_bntobcd_1_s0, codeur_bntobcd_1_s1, codeur_bntobcd_1_s2, codeur_bntobcd_1_s3,
       codeur_bntobcd_1_s4, codeur_bntobcd_1_s5, codeur_bntobcd_1_s6, codeur_bntobcd_1_s7, decodeur_4to7_1_a,
       decodeur_4to7_1_b, decodeur_4to7_1_c, decodeur_4to7_1_d, decodeur_4to7_1_e, decodeur_4to7_1_f,
       decodeur_4to7_1_g, decodeur_4to7_2_a, decodeur_4to7_2_b, decodeur_4to7_2_c, decodeur_4to7_2_d,
       decodeur_4to7_2_e, decodeur_4to7_2_f, decodeur_4to7_2_g;
  wire [3:0] add4b_1_s, dipswitch_1_sw1, dipswitch_2_sw1;

  DipSwitch #(.number(4)) dipswitch_1 (
    .sw1(dipswitch_1_sw1[0]), .sw2(dipswitch_1_sw1[1]), .sw3(dipswitch_1_sw1[2]), .sw4(dipswitch_1_sw1[3]));
  DipSwitch #(.number(4)) dipswitch_2 (
    .sw1(dipswitch_2_sw1[0]), .sw2(dipswitch_2_sw1[1]), .sw3(dipswitch_2_sw1[2]), .sw4(dipswitch_2_sw1[3]));
  add4b add4b_1 (.Cin(1'b0), .A(dipswitch_1_sw1), .B(dipswitch_2_sw1), .S(add4b_1_s));  // open: Cout
  codeur_BNtoBCD codeur_bntobcd_1 (
    .i7(1'b0), .i8(1'b0), .i9(1'b0), .i6(1'b0), .i5(1'b0), .i4(1'b0), .i3(add4b_1_s[3]), .i2(add4b_1_s[2]),
    .i1(add4b_1_s[1]), .i0(add4b_1_s[0]), .s0(codeur_bntobcd_1_s0), .s1(codeur_bntobcd_1_s1),
    .s5(codeur_bntobcd_1_s5), .s2(codeur_bntobcd_1_s2), .s6(codeur_bntobcd_1_s6), .s3(codeur_bntobcd_1_s3),
    .s7(codeur_bntobcd_1_s7), .s4(codeur_bntobcd_1_s4));  // open: s9, s13, s10, s14, s11, s15, s8, s12
  decodeur_4to7 decodeur_4to7_1 (
    .i0(codeur_bntobcd_1_s0), .i1(codeur_bntobcd_1_s1), .i2(codeur_bntobcd_1_s2), .i3(codeur_bntobcd_1_s3),
    .a(decodeur_4to7_1_a), .b(decodeur_4to7_1_b), .c(decodeur_4to7_1_c), .d(decodeur_4to7_1_d),
    .e(decodeur_4to7_1_e), .f(decodeur_4to7_1_f), .g(decodeur_4to7_1_g));
  decodeur_4to7 decodeur_4to7_2 (
    .i0(codeur_bntobcd_1_s4), .i1(codeur_bntobcd_1_s5), .i2(codeur_bntobcd_1_s6), .i3(codeur_bntobcd_1_s7),
    .a(decodeur_4to7_2_a), .b(decodeur_4to7_2_b), .c(decodeur_4to7_2_c), .d(decodeur_4to7_2_d),
    .e(decodeur_4to7_2_e), .f(decodeur_4to7_2_f), .g(decodeur_4to7_2_g));
  _7_Segment_Display u_7_segment_display_1 (
    .g(decodeur_4to7_1_g), .f(decodeur_4to7_1_f), .a(decodeur_4to7_1_a), .b(decodeur_4to7_1_b),
    .e(decodeur_4to7_1_e), .d(decodeur_4to7_1_d), .c(decodeur_4to7_1_c));  // open: dp
  _7_Segment_Display u_7_segment_display_2 (
    .g(decodeur_4to7_2_g), .f(decodeur_4to7_2_f), .a(decodeur_4to7_2_a), .b(decodeur_4to7_2_b),
    .e(decodeur_4to7_2_e), .d(decodeur_4to7_2_d), .c(decodeur_4to7_2_c));  // open: dp
endmodule

module and4b (
  input  [3:0] A,
  input  [3:0] B,
  output [3:0] S
);

  assign S = A & B;  // AND_Gate and_1, 4 bits wide
endmodule

module or4b (
  input  [3:0] A,
  input  [3:0] B,
  output [3:0] S
);

  assign S = A | B;  // OR_Gate or_1, 4 bits wide
endmodule

module not4b (
  input  [3:0] A,
  output [3:0] s
);

  assign s = ~A;  // NOT_Gate not_1, 4 bits wide
endmodule

module xor4b (
  input  [3:0] A,
  input  [3:0] B,
  output [3:0] S
);

  assign S = A ^ B;  // XOR_Gate xor_1, 4 bits wide
endmodule

module sub4b (
  input  [3:0] A,
  input  [3:0] B,
  output [3:0] S
);

  wire [3:0] not4b_1_s;

  not4b not4b_1 (.A(B), .s(not4b_1_s));
  add4b add4b_1 (.Cin(1'b1), .A(A), .B(not4b_1_s), .S(S));  // open: Cout
endmodule

module test_sub4b (
);

  wire codeur_bntobcd_1_s0, codeur_bntobcd_1_s1, codeur_bntobcd_1_s2, codeur_bntobcd_1_s3,
       codeur_bntobcd_1_s4, codeur_bntobcd_1_s5, codeur_bntobcd_1_s6, codeur_bntobcd_1_s7, decodeur_4to7_1_a,
       decodeur_4to7_1_b, decodeur_4to7_1_c, decodeur_4to7_1_d, decodeur_4to7_1_e, decodeur_4to7_1_f,
       decodeur_4to7_1_g, decodeur_4to7_2_a, decodeur_4to7_2_b, decodeur_4to7_2_c, decodeur_4to7_2_d,
       decodeur_4to7_2_e, decodeur_4to7_2_f, decodeur_4to7_2_g;
  wire [3:0] dipswitch_1_sw1, dipswitch_2_sw1, sub4b_1_s;

  DipSwitch #(.number(4)) dipswitch_1 (
    .sw1(dipswitch_1_sw1[0]), .sw2(dipswitch_1_sw1[1]), .sw3(dipswitch_1_sw1[2]), .sw4(dipswitch_1_sw1[3]));
  DipSwitch #(.number(4)) dipswitch_2 (
    .sw1(dipswitch_2_sw1[0]), .sw2(dipswitch_2_sw1[1]), .sw3(dipswitch_2_sw1[2]), .sw4(dipswitch_2_sw1[3]));
  sub4b sub4b_1 (.A(dipswitch_1_sw1), .B(dipswitch_2_sw1), .S(sub4b_1_s));
  codeur_BNtoBCD codeur_bntobcd_1 (
    .i7(1'b0), .i8(1'b0), .i9(1'b0), .i6(1'b0), .i5(1'b0), .i4(1'b0), .i3(sub4b_1_s[3]), .i2(sub4b_1_s[2]),
    .i1(sub4b_1_s[1]), .i0(sub4b_1_s[0]), .s0(codeur_bntobcd_1_s0), .s1(codeur_bntobcd_1_s1),
    .s5(codeur_bntobcd_1_s5), .s2(codeur_bntobcd_1_s2), .s6(codeur_bntobcd_1_s6), .s3(codeur_bntobcd_1_s3),
    .s7(codeur_bntobcd_1_s7), .s4(codeur_bntobcd_1_s4));  // open: s9, s13, s10, s14, s11, s15, s8, s12
  decodeur_4to7 decodeur_4to7_1 (
    .i0(codeur_bntobcd_1_s0), .i1(codeur_bntobcd_1_s1), .i2(codeur_bntobcd_1_s2), .i3(codeur_bntobcd_1_s3),
    .a(decodeur_4to7_1_a), .b(decodeur_4to7_1_b), .c(decodeur_4to7_1_c), .d(decodeur_4to7_1_d),
    .e(decodeur_4to7_1_e), .f(decodeur_4to7_1_f), .g(decodeur_4to7_1_g));
  decodeur_4to7 decodeur_4to7_2 (
    .i0(codeur_bntobcd_1_s4), .i1(codeur_bntobcd_1_s5), .i2(codeur_bntobcd_1_s6), .i3(codeur_bntobcd_1_s7),
    .a(decodeur_4to7_2_a), .b(decodeur_4to7_2_b), .c(decodeur_4to7_2_c), .d(decodeur_4to7_2_d),
    .e(decodeur_4to7_2_e), .f(decodeur_4to7_2_f), .g(decodeur_4to7_2_g));
  _7_Segment_Display u_7_segment_display_1 (
    .g(decodeur_4to7_1_g), .f(decodeur_4to7_1_f), .a(decodeur_4to7_1_a), .b(decodeur_4to7_1_b),
    .e(decodeur_4to7_1_e), .d(decodeur_4to7_1_d), .c(decodeur_4to7_1_c));  // open: dp
  _7_Segment_Display u_7_segment_display_2 (
    .g(decodeur_4to7_2_g), .f(decodeur_4to7_2_f), .a(decodeur_4to7_2_a), .b(decodeur_4to7_2_b),
    .e(decodeur_4to7_2_e), .d(decodeur_4to7_2_d), .c(decodeur_4to7_2_c));  // open: dp
endmodule

module mult4b (
  input  [3:0] A,
  output [3:0] S
);


  assign S = {A[2:0], 1'b0};
endmodule

module test_mult4b (
);

  wire codeur_bntobcd_1_s0, codeur_bntobcd_1_s1, codeur_bntobcd_1_s2, codeur_bntobcd_1_s3,
       codeur_bntobcd_1_s4, codeur_bntobcd_1_s5, codeur_bntobcd_1_s6, codeur_bntobcd_1_s7, decodeur_4to7_1_a,
       decodeur_4to7_1_b, decodeur_4to7_1_c, decodeur_4to7_1_d, decodeur_4to7_1_e, decodeur_4to7_1_f,
       decodeur_4to7_1_g, decodeur_4to7_2_a, decodeur_4to7_2_b, decodeur_4to7_2_c, decodeur_4to7_2_d,
       decodeur_4to7_2_e, decodeur_4to7_2_f, decodeur_4to7_2_g;
  wire [3:0] dipswitch_1_sw1, mult4b_1_s;

  DipSwitch #(.number(4)) dipswitch_1 (
    .sw1(dipswitch_1_sw1[0]), .sw2(dipswitch_1_sw1[1]), .sw3(dipswitch_1_sw1[2]), .sw4(dipswitch_1_sw1[3]));
  mult4b mult4b_1 (.A(dipswitch_1_sw1), .S(mult4b_1_s));
  codeur_BNtoBCD codeur_bntobcd_1 (
    .i7(1'b0), .i8(1'b0), .i9(1'b0), .i6(1'b0), .i5(1'b0), .i4(1'b0), .i3(mult4b_1_s[3]), .i2(mult4b_1_s[2]),
    .i1(mult4b_1_s[1]), .i0(mult4b_1_s[0]), .s0(codeur_bntobcd_1_s0), .s1(codeur_bntobcd_1_s1),
    .s5(codeur_bntobcd_1_s5), .s2(codeur_bntobcd_1_s2), .s6(codeur_bntobcd_1_s6), .s3(codeur_bntobcd_1_s3),
    .s7(codeur_bntobcd_1_s7), .s4(codeur_bntobcd_1_s4));  // open: s9, s13, s10, s14, s11, s15, s8, s12
  decodeur_4to7 decodeur_4to7_1 (
    .i0(codeur_bntobcd_1_s0), .i1(codeur_bntobcd_1_s1), .i2(codeur_bntobcd_1_s2), .i3(codeur_bntobcd_1_s3),
    .a(decodeur_4to7_1_a), .b(decodeur_4to7_1_b), .c(decodeur_4to7_1_c), .d(decodeur_4to7_1_d),
    .e(decodeur_4to7_1_e), .f(decodeur_4to7_1_f), .g(decodeur_4to7_1_g));
  decodeur_4to7 decodeur_4to7_2 (
    .i0(codeur_bntobcd_1_s4), .i1(codeur_bntobcd_1_s5), .i2(codeur_bntobcd_1_s6), .i3(codeur_bntobcd_1_s7),
    .a(decodeur_4to7_2_a), .b(decodeur_4to7_2_b), .c(decodeur_4to7_2_c), .d(decodeur_4to7_2_d),
    .e(decodeur_4to7_2_e), .f(decodeur_4to7_2_f), .g(decodeur_4to7_2_g));
  _7_Segment_Display u_7_segment_display_1 (
    .g(decodeur_4to7_1_g), .f(decodeur_4to7_1_f), .a(decodeur_4to7_1_a), .b(decodeur_4to7_1_b),
    .e(decodeur_4to7_1_e), .d(decodeur_4to7_1_d), .c(decodeur_4to7_1_c));  // open: dp
  _7_Segment_Display u_7_segment_display_2 (
    .g(decodeur_4to7_2_g), .f(decodeur_4to7_2_f), .a(decodeur_4to7_2_a), .b(decodeur_4to7_2_b),
    .e(decodeur_4to7_2_e), .d(decodeur_4to7_2_d), .c(decodeur_4to7_2_c));  // open: dp
endmodule

module div4b (
  input  [3:0] A,
  output [3:0] S
);


  assign S = {{2{A[3]}}, A[2:1]};
endmodule

module test_div4b (
);

  wire codeur_bntobcd_1_s0, codeur_bntobcd_1_s1, codeur_bntobcd_1_s2, codeur_bntobcd_1_s3,
       codeur_bntobcd_1_s4, codeur_bntobcd_1_s5, codeur_bntobcd_1_s6, codeur_bntobcd_1_s7, decodeur_4to7_1_a,
       decodeur_4to7_1_b, decodeur_4to7_1_c, decodeur_4to7_1_d, decodeur_4to7_1_e, decodeur_4to7_1_f,
       decodeur_4to7_1_g, decodeur_4to7_2_a, decodeur_4to7_2_b, decodeur_4to7_2_c, decodeur_4to7_2_d,
       decodeur_4to7_2_e, decodeur_4to7_2_f, decodeur_4to7_2_g;
  wire [3:0] dipswitch_1_sw1, div4b_1_s;

  DipSwitch #(.number(4)) dipswitch_1 (
    .sw1(dipswitch_1_sw1[0]), .sw2(dipswitch_1_sw1[1]), .sw3(dipswitch_1_sw1[2]), .sw4(dipswitch_1_sw1[3]));
  div4b div4b_1 (.A(dipswitch_1_sw1), .S(div4b_1_s));
  codeur_BNtoBCD codeur_bntobcd_1 (
    .i7(1'b0), .i8(1'b0), .i9(1'b0), .i6(1'b0), .i5(1'b0), .i4(1'b0), .i3(div4b_1_s[3]), .i2(div4b_1_s[2]),
    .i1(div4b_1_s[1]), .i0(div4b_1_s[0]), .s0(codeur_bntobcd_1_s0), .s1(codeur_bntobcd_1_s1),
    .s5(codeur_bntobcd_1_s5), .s2(codeur_bntobcd_1_s2), .s6(codeur_bntobcd_1_s6), .s3(codeur_bntobcd_1_s3),
    .s7(codeur_bntobcd_1_s7), .s4(codeur_bntobcd_1_s4));  // open: s9, s13, s10, s14, s11, s15, s8, s12
  decodeur_4to7 decodeur_4to7_1 (
    .i0(codeur_bntobcd_1_s0), .i1(codeur_bntobcd_1_s1), .i2(codeur_bntobcd_1_s2), .i3(codeur_bntobcd_1_s3),
    .a(decodeur_4to7_1_a), .b(decodeur_4to7_1_b), .c(decodeur_4to7_1_c), .d(decodeur_4to7_1_d),
    .e(decodeur_4to7_1_e), .f(decodeur_4to7_1_f), .g(decodeur_4to7_1_g));
  decodeur_4to7 decodeur_4to7_2 (
    .i0(codeur_bntobcd_1_s4), .i1(codeur_bntobcd_1_s5), .i2(codeur_bntobcd_1_s6), .i3(codeur_bntobcd_1_s7),
    .a(decodeur_4to7_2_a), .b(decodeur_4to7_2_b), .c(decodeur_4to7_2_c), .d(decodeur_4to7_2_d),
    .e(decodeur_4to7_2_e), .f(decodeur_4to7_2_f), .g(decodeur_4to7_2_g));
  _7_Segment_Display u_7_segment_display_1 (
    .g(decodeur_4to7_1_g), .f(decodeur_4to7_1_f), .a(decodeur_4to7_1_a), .b(decodeur_4to7_1_b),
    .e(decodeur_4to7_1_e), .d(decodeur_4to7_1_d), .c(decodeur_4to7_1_c));  // open: dp
  _7_Segment_Display u_7_segment_display_2 (
    .g(decodeur_4to7_2_g), .f(decodeur_4to7_2_f), .a(decodeur_4to7_2_a), .b(decodeur_4to7_2_b),
    .e(decodeur_4to7_2_e), .d(decodeur_4to7_2_d), .c(decodeur_4to7_2_c));  // open: dp
endmodule

module UAL (
  input  [3:0] A,
  input  [3:0] B,
  input  [2:0] Sel,
  output [3:0] S
);

  wire [3:0] add4b_1_s, and4b_1_s, div4b_1_s, mult4b_1_s, not4b_1_s, or4b_1_s, sub4b_1_s, xor4b_1_s;

  and4b and4b_1 (.A(A), .B(B), .S(and4b_1_s));
  or4b or4b_1 (.A(A), .B(B), .S(or4b_1_s));
  not4b not4b_1 (.A(A), .s(not4b_1_s));
  xor4b xor4b_1 (.A(A), .B(B), .S(xor4b_1_s));
  add4b add4b_1 (.Cin(1'b0), .A(A), .B(B), .S(add4b_1_s));  // open: Cout
  sub4b sub4b_1 (.A(A), .B(B), .S(sub4b_1_s));
  mult4b mult4b_1 (.A(A), .S(mult4b_1_s));
  div4b div4b_1 (.A(A), .S(div4b_1_s));
  Multiplexer #(.select(3), .width(4), .enable("false")) multiplexer_1 (
    .in0(and4b_1_s), .in1(or4b_1_s), .in2(not4b_1_s), .in3(xor4b_1_s), .in4(add4b_1_s), .in5(sub4b_1_s),
    .in6(mult4b_1_s), .in7(div4b_1_s), .out(S), .sel(Sel));
endmodule

module test_UAL (
);

  wire COD_s0, COD_s1, COD_s2, COD_s3, COD_s4, COD_s5, COD_s6, COD_s7, DEC0_a, DEC0_b, DEC0_c, DEC0_d,
       DEC0_e, DEC0_f, DEC0_g, DEC1_a, DEC1_b, DEC1_c, DEC1_d, DEC1_e, DEC1_f, DEC1_g;
  wire [2:0] Sel_sw1;
  wire [3:0] A_sw1, B_sw1, UAL__s;

  DipSwitch #(.number(4)) A (.sw1(A_sw1[0]), .sw2(A_sw1[1]), .sw3(A_sw1[2]), .sw4(A_sw1[3]));
  DipSwitch #(.number(4)) B (.sw1(B_sw1[0]), .sw2(B_sw1[1]), .sw3(B_sw1[2]), .sw4(B_sw1[3]));
  DipSwitch #(.number(3)) Sel (.sw1(Sel_sw1[0]), .sw2(Sel_sw1[1]), .sw3(Sel_sw1[2]));
  UAL UAL_ (.A(A_sw1), .B(B_sw1), .Sel(Sel_sw1), .S(UAL__s));
  codeur_BNtoBCD COD (
    .i7(1'b0), .i8(1'b0), .i9(1'b0), .i6(1'b0), .i5(1'b0), .i4(1'b0), .i3(UAL__s[3]), .i2(UAL__s[2]),
    .i1(UAL__s[1]), .i0(UAL__s[0]), .s0(COD_s0), .s1(COD_s1), .s5(COD_s5), .s2(COD_s2), .s6(COD_s6),
    .s3(COD_s3), .s7(COD_s7), .s4(COD_s4));  // open: s9, s13, s10, s14, s11, s15, s8, s12
  decodeur_4to7 DEC0 (
    .i0(COD_s0), .i1(COD_s1), .i2(COD_s2), .i3(COD_s3), .a(DEC0_a), .b(DEC0_b), .c(DEC0_c), .d(DEC0_d),
    .e(DEC0_e), .f(DEC0_f), .g(DEC0_g));
  decodeur_4to7 DEC1 (
    .i0(COD_s4), .i1(COD_s5), .i2(COD_s6), .i3(COD_s7), .a(DEC1_a), .b(DEC1_b), .c(DEC1_c), .d(DEC1_d),
    .e(DEC1_e), .f(DEC1_f), .g(DEC1_g));
  _7_Segment_Display L_7_Segment_Display_1 (
    .g(DEC0_g), .f(DEC0_f), .a(DEC0_a), .b(DEC0_b), .e(DEC0_e), .d(DEC0_d), .c(DEC0_c), .dp(1'b0));
  _7_Segment_Display L_7_Segment_Display_2 (
    .g(DEC1_g), .f(DEC1_f), .a(DEC1_a), .b(DEC1_b), .e(DEC1_e), .d(DEC1_d), .c(DEC1_c), .dp(1'b0));
endmodule

module inc6 (
  input  [5:0] A,
  output [5:0] S
);

  wire and_1_out, and_2_out, and_3_out, and_4_out;

  and and_1 (and_1_out, A[4], A[3], A[2], A[1], A[0]);
  xor xor_1 (S[5], A[5], and_1_out);
  and and_2 (and_2_out, A[3], A[2], A[1], A[0]);
  xor xor_2 (S[4], A[4], and_2_out);
  and and_3 (and_3_out, A[1], A[0]);
  and and_4 (and_4_out, A[2], A[1], A[0]);
  xor xor_3 (S[3], A[3], and_4_out);
  xor xor_4 (S[2], A[2], and_3_out);
  not not_1 (S[0], A[0]);
  xor xor_5 (S[1], A[1], A[0]);
endmodule

module equal6 (
  input  [5:0] A,
  input  [5:0] B,
  output AEqB
);

  wire [5:0] xnor_1_out;

  assign xnor_1_out = ~(A ^ B);  // XNOR_Gate xnor_1, 6 bits wide
  and and_1 (AEqB, xnor_1_out[0], xnor_1_out[1], xnor_1_out[2], xnor_1_out[3], xnor_1_out[4], xnor_1_out[5]);
endmodule

module test_equal6 (
);

  wire Eq6_aeqb;
  wire [5:0] A_sw6, B_sw6;

  DipSwitch #(.number(6)) A (
    .sw1(A_sw6[5]), .sw2(A_sw6[4]), .sw3(A_sw6[3]), .sw4(A_sw6[2]), .sw5(A_sw6[1]), .sw6(A_sw6[0]));
  DipSwitch #(.number(6)) B (
    .sw1(B_sw6[5]), .sw2(B_sw6[4]), .sw3(B_sw6[3]), .sw4(B_sw6[2]), .sw5(B_sw6[1]), .sw6(B_sw6[0]));
  equal6 Eq6 (.A(A_sw6), .B(B_sw6), .AEqB(Eq6_aeqb));
  LED AEqB (.in(Eq6_aeqb));
endmodule

module test_inc6 (
);

  wire n7_segment_display_1_p1, n7_segment_display_2_p1;
  wire [5:0] dipswitch_1_sw6, inc6_1_s;

  DipSwitch #(.number(6)) dipswitch_1 (
    .sw1(dipswitch_1_sw6[5]), .sw2(dipswitch_1_sw6[4]), .sw3(dipswitch_1_sw6[3]), .sw4(dipswitch_1_sw6[2]),
    .sw5(dipswitch_1_sw6[1]), .sw6(dipswitch_1_sw6[0]));
  inc6 inc6_1 (.A(dipswitch_1_sw6), .S(inc6_1_s));
  // Binary_to_BCD_converter binary_to_bcd_converter_1: pin names not known
  // BCD_to_7_Segment_decoder bcd_to_7_segment_decoder_1: pin names not known
  // _7_Segment_Display 7_segment_display_1: pin names not known; wires that end beside it: n7_segment_display_1_p1, n7_segment_display_1_p1
  // _7_Segment_Display 7_segment_display_2: pin names not known; wires that end beside it: n7_segment_display_2_p1, n7_segment_display_2_p1
  // BCD_to_7_Segment_decoder bcd_to_7_segment_decoder_2: pin names not known
endmodule

module cpt6 (
  input  [5:0] set,
  input  inc,
  input  clk,
  input  reset,
  output [5:0] out_5
);

  wire or_1_out;
  wire [5:0] inc6_1_s, multiplexer_1_out;

  or or_1 (or_1_out, set[5], set[4], set[3], set[2], set[1], set[0]);
  Multiplexer #(.width(6), .enable("false")) multiplexer_1 (
    .in0(inc6_1_s), .in1(set), .out(multiplexer_1_out), .sel(or_1_out));
  Register #(.width(6)) register_1 (.D(multiplexer_1_out), .en(inc), .clk(clk), .Q(out_5), .clr(reset));
  inc6 inc6_1 (.A(out_5), .S(inc6_1_s));
endmodule

module test_cpt6 (
  input  [5:0] in_1,
  output [5:0] out_2
);

  wire dipswitch_1_sw1, dipswitch_1_sw2;

  DipSwitch #(.number(2)) dipswitch_1 (.sw1(dipswitch_1_sw1), .sw2(dipswitch_1_sw2));
  cpt6 cpt6_1 (.set(in_1), .inc(dipswitch_1_sw1), .clk(dipswitch_1_sw2), .out_5(out_2));  // open: reset
endmodule

module cpt6modP (
  input  [5:0] P,
  input  inc,
  input  clk,
  input  reset,
  output [5:0] S
);

  wire equal6_1_p3;
  wire [5:0] inc6_1_s, multiplexer_1_out;

  Register #(.width(6)) register_1 (.D(multiplexer_1_out), .en(inc), .clk(clk), .Q(S), .clr(reset));
  inc6 inc6_1 (.A(S), .S(inc6_1_s));
  Multiplexer #(.width(6), .enable("false")) multiplexer_1 (
    .in0(inc6_1_s), .in1({6{1'b0}}), .out(multiplexer_1_out), .sel(equal6_1_p3));
  // equal6 equal6_1: pin names not known; wires that end beside it: inc6_1_s, P, equal6_1_p3
endmodule

module test_cpt6modP (
  input  [5:0] P,
  input  inc,
  input  rst,
  output [5:0] S
);

  wire clk_out;

  Clock sysclk ();  // open: out
  Clock clk (.out(clk_out));
  cpt6modP cpt6modp_1 (.P(P), .inc(inc), .clk(clk_out), .reset(rst), .S(S));
endmodule

module digital_watch (
  input  btn2,
  input  inc,
  input  btn1,
  input  clk,
  input  rst,
  output [5:0] ss,
  output [5:0] hh,
  output [5:0] mm
);

  wire and_1_out, bcd_to_7_segment_decoder_2_p1, bcd_to_7_segment_decoder_4_p1,
       bcd_to_7_segment_decoder_5_p1, binary_to_bcd_converter_1_p2, binary_to_bcd_converter_2_p2,
       binary_to_bcd_converter_3_p2, equal6_1_p3, equal6_2_p3, equal6_3_p3, or_1_out, or_2_out, xor_1_out,
       xor_2_out;

  or or_1 (or_1_out, and_1_out, xor_1_out);
  xor xor_1 (xor_1_out, btn2, clk);
  cpt6modP cpt6modp_1 (.P(6'b011000), .inc(or_1_out), .clk(clk), .reset(rst), .S(hh));
  // BCD_to_7_Segment_decoder bcd_to_7_segment_decoder_1: pin names not known
  _7_Segment_Display u_7_segment_display_1 ();  // open: g, f, a, b, e, d, c, dp
  // BCD_to_7_Segment_decoder bcd_to_7_segment_decoder_2: pin names not known; wires that end beside it: bcd_to_7_segment_decoder_2_p1
  _7_Segment_Display u_7_segment_display_2 ();  // open: g, f, a, b, e, d, c, dp
  // Binary_to_BCD_converter #(.binvalue(6)) binary_to_bcd_converter_1: pin names not known; wires that end beside it: hh, binary_to_bcd_converter_1_p2, binary_to_bcd_converter_1_p2, bcd_to_7_segment_decoder_2_p1
  and and_1 (and_1_out, equal6_1_p3, equal6_2_p3);
  xor xor_2 (xor_2_out, btn1, clk);
  or or_2 (or_2_out, equal6_3_p3, xor_2_out);
  cpt6modP cpt6modp_2 (.P(6'b111100), .inc(or_2_out), .clk(clk), .reset(rst), .S(mm));
  // equal6 equal6_1: pin names not known; wires that end beside it: {6{1'b0}}, ss, equal6_1_p3
  _7_Segment_Display u_7_segment_display_3 ();  // open: g, f, a, b, e, d, c, dp
  _7_Segment_Display u_7_segment_display_4 ();  // open: g, f, a, b, e, d, c, dp
  // BCD_to_7_Segment_decoder bcd_to_7_segment_decoder_3: pin names not known
  // BCD_to_7_Segment_decoder bcd_to_7_segment_decoder_4: pin names not known; wires that end beside it: bcd_to_7_segment_decoder_4_p1
  // Binary_to_BCD_converter #(.binvalue(6)) binary_to_bcd_converter_2: pin names not known; wires that end beside it: mm, binary_to_bcd_converter_2_p2, binary_to_bcd_converter_2_p2, bcd_to_7_segment_decoder_4_p1
  // equal6 equal6_2: pin names not known; wires that end beside it: 6'b111011, mm, equal6_2_p3
  cpt6modP cpt6modp_3 (.P(6'b111100), .inc(inc), .clk(clk), .reset(rst), .S(ss));
  // equal6 equal6_3: pin names not known; wires that end beside it: 6'b111011, ss, equal6_3_p3
  _7_Segment_Display u_7_segment_display_5 ();  // open: g, f, a, b, e, d, c, dp
  // BCD_to_7_Segment_decoder bcd_to_7_segment_decoder_5: pin names not known; wires that end beside it: bcd_to_7_segment_decoder_5_p1
  _7_Segment_Display u_7_segment_display_6 ();  // open: g, f, a, b, e, d, c, dp
  // BCD_to_7_Segment_decoder bcd_to_7_segment_decoder_6: pin names not known
  // Binary_to_BCD_converter #(.binvalue(6)) binary_to_bcd_converter_3: pin names not known; wires that end beside it: ss, binary_to_bcd_converter_3_p2, binary_to_bcd_converter_3_p2, bcd_to_7_segment_decoder_5_p1
endmodule

module bonus (
  input  inc,
  input  rst,
  output [5:0] ss,
  output [5:0] mm,
  output [5:0] hh
);

  wire and_1_out, btn_hh_out, btn_mm_out, clk, demultiplexer_1_out0, demultiplexer_1_out1,
       demultiplexer_1_out2, demultiplexer_1_out3, demultiplexer_2_out0, demultiplexer_2_out1,
       demultiplexer_2_out2, demultiplexer_2_out3, equal6_1_p3, equal6_2_p3, equal6_3_p3, multiplexer_4_out,
       n7_segment_display_1_p1, n7_segment_display_2_p1, n7_segment_display_3_p1, n7_segment_display_4_p1,
       n7_segment_display_5_p1, n7_segment_display_6_p1, or_1_out, or_2_out, or_3_out, or_4_out, or_5_out,
       xor_1_out, xor_2_out, xor_3_out, xor_4_out;
  wire [1:0] mode_sw2;
  wire [5:0] hh_mode00_01, mm_mode00_01, reveil_hh_s, reveil_mm_s, ss_mode00_01;

  Clock sysclk ();  // open: out
  Clock u_clk (.out(clk));
  digital_watch mode_00_01 (
    .btn2(or_2_out), .inc(inc), .btn1(or_4_out), .clk(clk), .rst(rst), .ss(ss_mode00_01), .hh(hh_mode00_01),
    .mm(mm_mode00_01));
  or or_1 (or_1_out, equal6_1_p3, or_3_out);
  or or_2 (or_2_out, xor_1_out, demultiplexer_1_out1);
  cpt6modP reveil_hh (.P(6'b011000), .inc(or_1_out), .clk(clk), .reset(rst), .S(reveil_hh_s));
  Button btn_hh (.out(btn_hh_out));
  Demultiplexer #(.select(2), .enable("false")) demultiplexer_1 (
    .out0(demultiplexer_1_out0), .out1(demultiplexer_1_out1), .out2(demultiplexer_1_out2),
    .out3(demultiplexer_1_out3), .in(btn_hh_out), .sel(mode_sw2));
  xor xor_1 (xor_1_out, demultiplexer_1_out0, demultiplexer_1_out0);
  xor xor_2 (xor_2_out, demultiplexer_1_out3, demultiplexer_1_out3);
  DipSwitch #(.number(2)) mode (.sw1(mode_sw2[1]), .sw2(mode_sw2[0]));
  or or_3 (or_3_out, xor_2_out, demultiplexer_1_out2);
  or or_4 (or_4_out, xor_3_out, demultiplexer_2_out1);
  xor xor_3 (xor_3_out, demultiplexer_2_out0, demultiplexer_2_out0);
  Demultiplexer #(.select(2), .enable("false")) demultiplexer_2 (
    .out0(demultiplexer_2_out0), .out1(demultiplexer_2_out1), .out2(demultiplexer_2_out2),
    .out3(demultiplexer_2_out3), .in(btn_mm_out), .sel(mode_sw2));
  Button btn_mm (.out(btn_mm_out));
  cpt6modP reveil_mm (.P(6'b111100), .inc(or_5_out), .clk(clk), .reset(rst), .S(reveil_mm_s));
  xor xor_4 (xor_4_out, demultiplexer_2_out3, demultiplexer_2_out3);
  or or_5 (or_5_out, xor_4_out, demultiplexer_2_out2);
  // equal6 equal6_1: pin names not known; wires that end beside it: 6'b111011, reveil_mm_s, equal6_1_p3
  // BCD_to_7_Segment_decoder bcd_to_7_segment_decoder_1: pin names not known
  // _7_Segment_Display 7_segment_display_1: pin names not known; wires that end beside it: n7_segment_display_1_p1, n7_segment_display_1_p1
  // Binary_to_BCD_converter #(.binvalue(6)) binary_to_bcd_converter_1: pin names not known; wires that end beside it: hh
  // BCD_to_7_Segment_decoder bcd_to_7_segment_decoder_2: pin names not known
  // _7_Segment_Display 7_segment_display_2: pin names not known; wires that end beside it: n7_segment_display_2_p1, n7_segment_display_2_p1
  Multiplexer #(.select(2), .width(6), .enable("false")) multiplexer_1 (
    .in0(ss_mode00_01), .in1(ss_mode00_01), .in2({6{1'b0}}), .in3(ss_mode00_01), .out(ss), .sel(mode_sw2));
  Multiplexer #(.select(2), .width(6), .enable("false")) multiplexer_2 (
    .in0(mm_mode00_01), .in1(mm_mode00_01), .in2(reveil_mm_s), .in3(mm_mode00_01), .out(mm), .sel(mode_sw2));
  Multiplexer #(.select(2), .width(6), .enable("false")) multiplexer_3 (
    .in0(hh_mode00_01), .in1(hh_mode00_01), .in2(reveil_hh_s), .in3(hh_mode00_01), .out(hh), .sel(mode_sw2));
  // _7_Segment_Display 7_segment_display_3: pin names not known; wires that end beside it: n7_segment_display_3_p1, n7_segment_display_3_p1
  // BCD_to_7_Segment_decoder bcd_to_7_segment_decoder_3: pin names not known; wires that end beside it: hh_mode00_01
  // Binary_to_BCD_converter #(.binvalue(6)) binary_to_bcd_converter_2: pin names not known; wires that end beside it: mm
  // equal6 equal6_2: pin names not known; wires that end beside it: hh_mode00_01, reveil_hh_s, equal6_2_p3
  and and_1 (and_1_out, equal6_2_p3, equal6_3_p3);
  // equal6 equal6_3: pin names not known; wires that end beside it: reveil_mm_s, mm_mode00_01, equal6_3_p3
  // BCD_to_7_Segment_decoder bcd_to_7_segment_decoder_4: pin names not known
  // _7_Segment_Display 7_segment_display_4: pin names not known; wires that end beside it: n7_segment_display_4_p1, n7_segment_display_4_p1
  Multiplexer #(.select(2), .enable("false")) multiplexer_4 (
    .in0(1'b0), .in1(1'b0), .in2(1'b0), .in3(and_1_out), .out(multiplexer_4_out), .sel(mode_sw2));
  // _7_Segment_Display 7_segment_display_5: pin names not known; wires that end beside it: n7_segment_display_5_p1, n7_segment_display_5_p1
  // BCD_to_7_Segment_decoder bcd_to_7_segment_decoder_5: pin names not known; wires that end beside it: mode_sw2[1]
  // _7_Segment_Display 7_segment_display_6: pin names not known; wires that end beside it: n7_segment_display_6_p1, n7_segment_display_6_p1
  // BCD_to_7_Segment_decoder bcd_to_7_segment_decoder_6: pin names not known
  // Binary_to_BCD_converter #(.binvalue(6)) binary_to_bcd_converter_3: pin names not known; wires that end beside it: ss
  LED wake_up (.in(multiplexer_4_out));
endmodule

module mode_00 (
  input  inc,
  input  rst,
  output [5:0] ss,
  output [5:0] hh,
  output [5:0] mm
);

  wire binary_to_bcd_converter_1_p2, binary_to_bcd_converter_1_p4, binary_to_bcd_converter_2_p2,
       binary_to_bcd_converter_2_p4, binary_to_bcd_converter_3_p2, binary_to_bcd_converter_3_p4;

  digital_watch digital_watch_1 (
    .btn2(1'b0), .inc(inc), .btn1(1'b0), .clk(rst), .ss(ss), .hh(hh), .mm(mm));  // open: rst
  _7_Segment_Display u_7_segment_display_1 ();  // open: g, f, a, b, e, d, c, dp
  // Bin_to_7_Segment_decoder bin_to_7_segment_decoder_1: pin names not known
  // Binary_to_BCD_converter #(.binvalue(6)) binary_to_bcd_converter_1: pin names not known; wires that end beside it: hh, binary_to_bcd_converter_1_p2, binary_to_bcd_converter_1_p2, binary_to_bcd_converter_1_p4
  _7_Segment_Display u_7_segment_display_2 ();  // open: g, f, a, b, e, d, c, dp
  // Bin_to_7_Segment_decoder bin_to_7_segment_decoder_2: pin names not known; wires that end beside it: binary_to_bcd_converter_1_p4
  // Bin_to_7_Segment_decoder bin_to_7_segment_decoder_3: pin names not known
  _7_Segment_Display u_7_segment_display_3 ();  // open: g, f, a, b, e, d, c, dp
  // Binary_to_BCD_converter #(.binvalue(6)) binary_to_bcd_converter_2: pin names not known; wires that end beside it: mm, binary_to_bcd_converter_2_p2, binary_to_bcd_converter_2_p2, binary_to_bcd_converter_2_p4
  // Bin_to_7_Segment_decoder bin_to_7_segment_decoder_4: pin names not known; wires that end beside it: binary_to_bcd_converter_2_p4
  _7_Segment_Display u_7_segment_display_4 ();  // open: g, f, a, b, e, d, c, dp
  // Bin_to_7_Segment_decoder bin_to_7_segment_decoder_5: pin names not known
  _7_Segment_Display u_7_segment_display_5 ();  // open: g, f, a, b, e, d, c, dp
  // Binary_to_BCD_converter #(.binvalue(6)) binary_to_bcd_converter_3: pin names not known; wires that end beside it: ss, binary_to_bcd_converter_3_p2, binary_to_bcd_converter_3_p2, binary_to_bcd_converter_3_p4
  _7_Segment_Display u_7_segment_display_6 ();  // open: g, f, a, b, e, d, c, dp
  // Bin_to_7_Segment_decoder bin_to_7_segment_decoder_6: pin names not known; wires that end beside it: binary_to_bcd_converter_3_p4
endmodule

module mode_01 (
  input  in_1,
  input  in_2
);

  wire binary_to_bcd_converter_1_p2, binary_to_bcd_converter_1_p4, binary_to_bcd_converter_2_p2,
       binary_to_bcd_converter_2_p4, binary_to_bcd_converter_3_p2, binary_to_bcd_converter_3_p4,
       button_1_out, button_2_out;
  wire [5:0] digital_watch_1_hh, digital_watch_1_mm, digital_watch_1_ss;

  Button button_1 (.out(button_1_out));
  Button button_2 (.out(button_2_out));
  digital_watch digital_watch_1 (
    .btn2(button_1_out), .inc(in_1), .btn1(button_2_out), .clk(in_2), .ss(digital_watch_1_ss),
    .hh(digital_watch_1_hh), .mm(digital_watch_1_mm));  // open: rst
  // Bin_to_7_Segment_decoder bin_to_7_segment_decoder_1: pin names not known
  _7_Segment_Display u_7_segment_display_1 ();  // open: g, f, a, b, e, d, c, dp
  // Binary_to_BCD_converter #(.binvalue(6)) binary_to_bcd_converter_1: pin names not known; wires that end beside it: digital_watch_1_hh, binary_to_bcd_converter_1_p2, binary_to_bcd_converter_1_p2, binary_to_bcd_converter_1_p4
  // Bin_to_7_Segment_decoder bin_to_7_segment_decoder_2: pin names not known; wires that end beside it: binary_to_bcd_converter_1_p4
  _7_Segment_Display u_7_segment_display_2 ();  // open: g, f, a, b, e, d, c, dp
  // Bin_to_7_Segment_decoder bin_to_7_segment_decoder_3: pin names not known
  _7_Segment_Display u_7_segment_display_3 ();  // open: g, f, a, b, e, d, c, dp
  // Binary_to_BCD_converter #(.binvalue(6)) binary_to_bcd_converter_2: pin names not known; wires that end beside it: digital_watch_1_mm, binary_to_bcd_converter_2_p2, binary_to_bcd_converter_2_p2, binary_to_bcd_converter_2_p4
  _7_Segment_Display u_7_segment_display_4 ();  // open: g, f, a, b, e, d, c, dp
  // Bin_to_7_Segment_decoder bin_to_7_segment_decoder_4: pin names not known; wires that end beside it: binary_to_bcd_converter_2_p4
  _7_Segment_Display u_7_segment_display_5 ();  // open: g, f, a, b, e, d, c, dp
  // Bin_to_7_Segment_decoder bin_to_7_segment_decoder_5: pin names not known
  // Binary_to_BCD_converter #(.binvalue(6)) binary_to_bcd_converter_3: pin names not known; wires that end beside it: digital_watch_1_ss, binary_to_bcd_converter_3_p2, binary_to_bcd_converter_3_p2, binary_to_bcd_converter_3_p4
  // Bin_to_7_Segment_decoder bin_to_7_segment_decoder_6: pin names not known; wires that end beside it: binary_to_bcd_converter_3_p4
  _7_Segment_Display u_7_segment_display_6 ();  // open: g, f, a, b, e, d, c, dp
endmodule

module mode_10 (
  input  btn1,
  input  btn2,
  input  rst,
  output [5:0] mm,
  output [5:0] hh
);

  wire bin_to_7_segment_decoder_2_p1, binary_to_bcd_converter_1_p2, binary_to_bcd_converter_2_p2,
       binary_to_bcd_converter_2_p4, clk, equal6_1_p3, or_1_out, xor_1_out, xor_2_out;

  Clock sysclk ();  // open: out
  or or_1 (or_1_out, equal6_1_p3, btn2);
  xor xor_1 (xor_1_out, or_1_out, clk);
  Clock clock_1 (.out(clk));
  cpt6modP cpt6modp_1 (.P(6'b011000), .inc(xor_1_out), .clk(clk), .reset(rst), .S(hh));
  xor xor_2 (xor_2_out, btn1, clk);
  cpt6modP cpt6modp_2 (.P(6'b111100), .inc(btn1), .clk(xor_2_out), .reset(rst), .S(mm));
  // equal6 equal6_1: pin names not known; wires that end beside it: 6'b111011, mm, equal6_1_p3
  // Bin_to_7_Segment_decoder bin_to_7_segment_decoder_1: pin names not known
  _7_Segment_Display u_7_segment_display_1 ();  // open: g, f, a, b, e, d, c, dp
  // Bin_to_7_Segment_decoder bin_to_7_segment_decoder_2: pin names not known; wires that end beside it: bin_to_7_segment_decoder_2_p1
  _7_Segment_Display u_7_segment_display_2 ();  // open: g, f, a, b, e, d, c, dp
  // Binary_to_BCD_converter #(.binvalue(6)) binary_to_bcd_converter_1: pin names not known; wires that end beside it: hh, binary_to_bcd_converter_1_p2, binary_to_bcd_converter_1_p2, bin_to_7_segment_decoder_2_p1
  _7_Segment_Display u_7_segment_display_3 ();  // open: g, f, a, b, e, d, c, dp
  // Bin_to_7_Segment_decoder bin_to_7_segment_decoder_3: pin names not known
  // Binary_to_BCD_converter #(.binvalue(6)) binary_to_bcd_converter_2: pin names not known; wires that end beside it: mm, binary_to_bcd_converter_2_p2, binary_to_bcd_converter_2_p2, binary_to_bcd_converter_2_p4
  // Bin_to_7_Segment_decoder bin_to_7_segment_decoder_4: pin names not known; wires that end beside it: binary_to_bcd_converter_2_p4
  _7_Segment_Display u_7_segment_display_4 ();  // open: g, f, a, b, e, d, c, dp
endmodule

module mode_11 (
);

  wire and_1_out, equal6_1_p3, equal6_2_p3;
  wire [5:0] mode_00_1_hh, mode_00_1_mm, mode_10_1_hh, mode_10_1_mm;

  mode_00 mode_00_1 (.hh(mode_00_1_hh), .mm(mode_00_1_mm));  // open: inc, rst, ss
  mode_10 mode_10_1 (.mm(mode_10_1_mm), .hh(mode_10_1_hh));  // open: btn1, btn2, rst
  // equal6 equal6_1: pin names not known; wires that end beside it: mode_00_1_mm, mode_10_1_mm, equal6_1_p3
  // equal6 equal6_2: pin names not known; wires that end beside it: mode_00_1_hh, mode_10_1_hh, equal6_2_p3
  and and_1 (and_1_out, equal6_1_p3, equal6_2_p3);
  LED wake_up (.in(and_1_out));
endmodule
