// Logisim project exercise.circ as structural Verilog
module CC20192020 (
  input  set,
  input  reset,
  output D2,
  output Q2,
  output Q1,
  output Q0
);

  wire clk_out;

  Clock sysclk ();  // open: out
  Clock clk (.out(clk_out));
  D_Flip_Flop D (.D(D2), .clk(clk_out), .Q(Q2), .preset(set), .reset(reset));  // open: Qn
  xor xor_1 (D2, Q1, Q0);
  D_Flip_Flop D1 (.D(Q2), .clk(clk_out), .Q(Q1), .preset(set), .reset(reset));  // open: Qn
  D_Flip_Flop D0 (.D(Q1), .clk(clk_out), .Q(Q0), .preset(set), .reset(reset));  // open: Qn
endmodule

module CC20202021 (
  input  [3:0] DIN,
  input  RST,
  output [3:0] DOUT4,
  output DOUT6,
  output [3:0] DOUT5,
  output DOUT3,
  output [3:0] DOUT2,
  output [3:0] DOUT1
);

  wire CLK;

  Clock sysclk ();  // open: out
  Clock u_clk (.out(CLK));
  Register #(.width(4)) R1 (.D(DIN), .en(1'b1), .clk(CLK), .Q(DOUT1), .clr(RST));
  Register #(.width(4)) R2 (.D(DOUT1), .en(1'b1), .clk(CLK), .Q(DOUT2), .clr(RST));
  Adder #(.width(4)) adder_1 (.a(DOUT1), .b(DOUT2), .out(DOUT4), .cin(1'b0), .cout(DOUT3));
  Register #(.width(4)) R3 (.D(DOUT4), .en(DOUT6), .clk(CLK), .Q(DOUT5), .clr(RST));
  Comparator #(.width(4)) comparator_1 (.a(DOUT4), .b(DOUT5), .gt(DOUT6));  // open: eq, lt
endmodule

module CC20202021exo3 (
  input  [7:0] C0,
  input  [3:0] in_2,
  input  RST,
  input  [7:0] C1,
  output [7:0] S
);

  wire clk_out;
  wire [3:0] register_1_q;
  wire [7:0] multiplier_1_out, multiplier_2_out;

  Clock sysclk ();  // open: out
  Register #(.width(4)) register_1 (.D(in_2), .en(1'b1), .clk(clk_out), .Q(register_1_q), .clr(RST));
  Clock clk (.out(clk_out));
  Multiplier multiplier_1 (.a({4'b0000, in_2}), .b(C0), .out(multiplier_1_out));  // open: cin, cout
  Multiplier multiplier_2 (.a({4'b0000, register_1_q}), .b(C1), .out(multiplier_2_out));  // open: cin, cout
  Adder adder_1 (.a(multiplier_1_out), .b(multiplier_2_out), .out(S), .cin(1'b0));  // open: cout
endmodule

module cc2021exo3UC (
);

  // FSM_Entity #(.content("state_machine example @[50,50,800,500]{\n	in In[4]   @[50,102,37,15];isDigit[1]   @[50,166,38,15];isD[1]   @[50,200,24,15];\n	out O1[1]   @[828,425,22,15];Out[4]   @[802,514,48,15];\n	codeWidth = 4;\n	reset = S0;\n	\n	state S0[\"0000\"]:\n	 	@[139,162,30,30]\n		set Out=\"1000\";O1=\"1\";  @[139,162,30,30]	\n		goto S1  when ((isDigit==\"1\").(isD==\"1\"))   @[196,213,140,24]; \n	state S1[\"0001\"]:\n	 	@[320,160,30,30]\n		set Out=\"0000\";  @[320,160,30,30]	\n		goto S2  when (isDigit==\"1\")   @[422,175,75,24]; \n	state S2[\"0010\"]:\n	 	@[512,164,30,30]\n		set Out=\"0000\";  @[512,164,30,30]	\n}")) fsm_entity_1: pin names not known
endmodule

module cc (
  input  CLK,
  input  WEA1,
  input  SEL1,
  input  rst,
  input  WE1,
  input  [1:0] A,
  input  [1:0] B,
  output [3:0] out_8
);

  wire multiplexer_1_out;
  wire [1:0] and_1_out, demultiplexer_1_out0, demultiplexer_1_out1, multiplexer_2_out, register_1_q,
       register_2_q;

  Multiplexer #(.enable("false")) multiplexer_1 (.in0(A[0]), .in1(A[1]), .out(multiplexer_1_out), .sel(SEL1));
  Multiplexer #(.width(2), .enable("false")) multiplexer_2 (.in0(B), .in1(B), .out(multiplexer_2_out), .sel(SEL1));
  and and_1 (and_1_out[0], multiplexer_1_out, multiplexer_2_out[0]);
  and and_2 (and_1_out[1], multiplexer_2_out[1], multiplexer_1_out);
  Demultiplexer #(.width(2), .enable("false")) demultiplexer_1 (
    .out0(demultiplexer_1_out0), .out1(demultiplexer_1_out1), .in(and_1_out), .sel(SEL1));
  Register #(.width(2)) register_1 (.D(demultiplexer_1_out0), .en(WEA1), .clk(CLK), .Q(register_1_q), .clr(rst));
  Register #(.width(2)) register_2 (.D(demultiplexer_1_out1), .en(WE1), .clk(CLK), .Q(register_2_q), .clr(rst));
  Adder #(.width(4)) adder_1 (
    .a({2'b00, register_1_q}), .b({1'b0, register_2_q, 1'b0}), .out(out_8), .cin(1'b0));  // open: cout
endmodule

module CC1 (
  input  [1:0] B,
  input  [1:0] A,
  output [3:0] out_3
);

  wire adder_1_cout;
  wire [0:0] multiplexer_3_out;
  wire [1:0] adder_1_out, multiplexer_4_out, multiplexer_5_out, multiplexer_6_out;
  wire [1:1] multiplexer_1_out, multiplexer_2_out;

  Multiplexer #(.enable("false")) multiplexer_1 (.in0(1'b0), .in1(1'b1), .out(multiplexer_1_out[1]), .sel(A[1]));
  Multiplexer #(.enable("false")) multiplexer_2 (.in0(1'b0), .in1(1'b1), .out(multiplexer_2_out[1]), .sel(A[1]));
  Multiplexer #(.enable("false")) multiplexer_3 (.in0(1'b0), .in1(1'b1), .out(multiplexer_3_out[0]), .sel(A[0]));
  Multiplexer #(.select(2), .width(2), .enable("false")) multiplexer_4 (
    .in0(2'b00), .in1(2'b00), .in2(2'b00), .in3({multiplexer_1_out[1], 1'b0}), .out(multiplexer_4_out),
    .sel(B));
  Multiplexer #(.select(2), .width(2), .enable("false")) multiplexer_5 (
    .in0(2'b00), .in1(2'b00), .in2(2'b00), .in3({multiplexer_2_out[1], 1'b0}), .out(multiplexer_5_out),
    .sel(B));
  Multiplexer #(.select(2), .width(2), .enable("false")) multiplexer_6 (
    .in0(2'b00), .in1(2'b00), .in2(2'b00), .in3({1'b0, multiplexer_3_out[0]}), .out(multiplexer_6_out),
    .sel(B));
  Adder #(.width(2)) adder_1 (
    .a(multiplexer_4_out), .b(multiplexer_5_out), .out(adder_1_out), .cin(1'b0), .cout(adder_1_cout));
  Adder #(.width(4)) adder_2 (
    .a({2'b00, adder_1_out}), .b({2'b00, multiplexer_6_out}), .out(out_3), .cin(adder_1_cout));  // open: cout
endmodule

module cc2 (
  input  rst,
  input  in_2,
  input  [2:0] in_3,
  input  [1:0] A,
  input  [1:0] B,
  output [3:0] out_6
);

  wire clk, fsm_entity_1_p6, fsm_entity_1_p7, fsm_entity_1_p8, sysclk_out;

  Clock sysclk (.out(sysclk_out));
  Clock u_clk (.out(clk));
  // FSM_Entity #(.content("state_machine example @[50,50,800,500]{\n	in A[3]   @[50,100,36,15];\n	out WEA1[1]   @[810,206,40,15];WE1[1]   @[818,270,32,15];SEL1[1]   @[815,320,35,15];\n	codeWidth = 2;\n	reset = S0;\n	\n	state S0[\"00\"]:\n	 	@[156,189,30,30]\n		set WEA1=\"0\";WE1=\"0\";SEL1=\"0\";  @[156,189,30,30]	\n		goto S1  when default   @[253,202,40,24]; \n	state S1[\"01\"]:\n	 	@[318,187,30,30]\n		set WEA1=\"1\";WE1=\"0\";SEL1=\"0\";  @[318,187,30,30]	\n		goto S2  when default   @[424,205,40,24]; \n	state S2[\"10\"]:\n	 	@[502,195,30,30]\n		set WEA1=\"0\";WE1=\"1\";SEL1=\"1\";  @[502,195,30,30]	\n		goto S0  when default   @[336,380,40,24]; \n}")) fsm_entity_1: pin names not known; wires that end beside it: sysclk_out, clk, rst, in_2, in_3, fsm_entity_1_p6, fsm_entity_1_p7, fsm_entity_1_p8
  cc cc_1 (
    .CLK(clk), .WEA1(fsm_entity_1_p6), .SEL1(fsm_entity_1_p8), .rst(rst), .WE1(fsm_entity_1_p7), .A(A),
    .B(B), .out_8(out_6));
endmodule
