// Logisim project TP6_SEN2.circ as structural Verilog: 6 circuits, main circuit Keypad_FSM
module Keypad_FSM (
  input  clk,
  input  rst,
  input  en,
  input  lhit,
  input  ack,
  output req,
  output WE,
  output [3:0] C
);

  // FSM_Entity #(.content("state_machine Keypad_FSM @[108,62,1000,800]{\n	in Lhit[1]   @[108,125,25,15];ACK[1]   @[108,166,30,15];\n	out REQ[1]   @[1077,637,31,15];WE[1]   @[1083,689,25,15];C0[4]   @[1063,717,45,15];\n	codeWidth = 4;\n	reset = E0;\n	\n	state E0[\"0000\"]:\n	 	@[188,197,30,30]\n		set C0=\"0000\";  @[188,197,30,30]	\n		goto E1  when default   @[288,213,42,24]; \n	state E1[\"0001\"]:\n	 	@[377,203,30,30]\n		set C0=\"0001\";REQ=\"0\";WE=\"0\";  @[377,203,30,30]	\n		goto E2  when (Lhit==\"0\")   @[488,217,62,24]; \n		goto E5  when (Lhit==\"1\")   @[392,275,62,24]; \n	state E2[\"0010\"]:\n	 	@[602,196,30,30]\n		set C0=\"0010\";REQ=\"0\";WE=\"0\";  @[602,196,30,30]	\n		goto E3  when (Lhit==\"0\")   @[692,220,62,24]; \n		goto E6  when (Lhit==\"1\")   @[617,275,62,24]; \n	state E3[\"0011\"]:\n	 	@[789,207,30,30]\n		set C0=\"0100\";REQ=\"0\";WE=\"0\";  @[789,207,30,30]	\n		goto E4  when (Lhit==\"0\")   @[860,222,62,24]; \n		goto E7  when (Lhit==\"1\")   @[803,277,62,24]; \n	state E4[\"0100\"]:\n	 	@[929,205,30,30]\n		set C0=\"1000\";REQ=\"0\";WE=\"0\";  @[929,205,30,30]	\n		goto E8  when (Lhit==\"1\")   @[947,275,62,24]; \n		goto E1  when (Lhit==\"0\")   @[668,111,62,24]; \n	state E5[\"0101\"]:\n	 	@[373,338,30,30]\n		set C0=\"0010\";REQ=\"1\";WE=\"1\";  @[373,338,30,30]	\n		goto E9  when default   @[376,401,42,24]; \n	state E6[\"0110\"]:\n	 	@[598,331,30,30]\n		set C0=\"0010\";REQ=\"1\";WE=\"1\";  @[598,331,30,30]	\n		goto E10  when default   @[591,390,42,24]; \n	state E7[\"0111\"]:\n	 	@[785,342,30,30]\n		set C0=\"0100\";REQ=\"1\";WE=\"1\";  @[785,342,30,30]	\n		goto E11  when default   @[794,399,42,24]; \n	state E8[\"1000\"]:\n	 	@[926,342,30,30]\n		set C0=\"1000\";REQ=\"1\";WE=\"1\";  @[926,342,30,30]	\n		goto E12  when default   @[943,400,42,24]; \n	state E9[\"1001\"]:\n	 	@[345,457,30,30]\n		set C0=\"0010\";REQ=\"1\";WE=\"0\";  @[345,457,30,30]	\n		goto E13  when ((ACK==\"1\").(Lhit==\"0\"))   @[363,534,135,24]; \n	state E10[\"1010\"]:\n	 	@[551,444,30,30]\n		set C0=\"0010\";REQ=\"1\";WE=\"0\";  @[551,444,30,30]	\n		goto E13  when ((ACK==\"1\").(Lhit==\"0\"))   @[470,530,135,24]; \n	state E11[\"1011\"]:\n	 	@[766,442,30,30]\n		set C0=\"0100\";REQ=\"1\";WE=\"0\";  @[766,442,30,30]	\n		goto E13  when ((ACK==\"1\").(Lhit==\"0\"))   @[581,532,135,24]; \n	state E12[\"1100\"]:\n	 	@[931,456,30,30]\n		set C0=\"1000\";REQ=\"1\";WE=\"0\";  @[931,456,30,30]	\n		goto E13  when ((ACK==\"1\").(Lhit==\"0\"))   @[705,577,135,24]; \n	state E13[\"1101\"]:\n	 	@[344,605,30,30]\n		set C0=\"0000\";REQ=\"0\";WE=\"0\";  @[344,605,30,30]	\n		goto E1  when (ACK==\"0\")   @[183,427,67,24]; \n}")) keypad_fsm_1: pin names not known; wires that end beside it: clk, rst, en, lhit, ack, req, WE, C
endmodule

module cltokey (
  input  C3,
  input  C2,
  input  C1,
  input  C0,
  input  L3,
  input  L2,
  input  L1,
  input  L0,
  output K3,
  output K2,
  output K1,
  output K0
);

  wire and_1_out, and_2_out, and_3_out, and_4_out, and_5_out, and_6_out, and_7_out, and_8_out, and_9_out,
       and_10_out, and_11_out, not_1_out, not_2_out, not_3_out, not_4_out, not_5_out, not_6_out, not_7_out,
       not_8_out, not_9_out;

  not not_1 (not_1_out, C0);
  and and_1 (and_1_out, not_1_out, L2);
  not not_2 (not_2_out, C1);
  and and_2 (and_2_out, not_2_out, L3);
  and and_3 (and_3_out, C0, L2);
  not not_3 (not_3_out, C0);
  and and_4 (and_4_out, not_3_out, L0);
  and and_5 (and_5_out, C0, not_4_out, not_5_out);
  not not_4 (not_4_out, L1);
  not not_5 (not_5_out, L0);
  and and_6 (and_6_out, C2, not_6_out);
  not not_6 (not_6_out, L2);
  and and_7 (and_7_out, C3, L1);
  not not_7 (not_7_out, C1);
  and and_8 (and_8_out, not_7_out, L0);
  not not_8 (not_8_out, C1);
  and and_9 (and_9_out, not_8_out, L2);
  and and_10 (and_10_out, C1, L1);
  and and_11 (and_11_out, C2, not_9_out);
  not not_9 (not_9_out, L1);
  or or_1 (K3, and_1_out, and_2_out, C3);
  or or_2 (K2, L1, and_3_out, C3);
  or or_3 (K1, and_4_out, and_5_out, and_6_out, and_7_out);
  or or_4 (K0, and_8_out, and_9_out, and_10_out, and_11_out);
endmodule

module Stockage (
  input  [3:0] Key,
  input  WE,
  input  CLK,
  input  RST,
  output [3:0] Key_out
);

  Register #(.width(4)) register_1 (.D(Key), .en(WE), .clk(CLK), .Q(Key_out), .clr(RST));
endmodule

module Detect_ligne (
  input  [3:0] L,
  output Lhit
);

  or or_1 (Lhit, L[0], L[1], L[2], L[3]);
endmodule

module test_keypad_decoder (
  input  clk,
  input  L,
  input  L_1,
  input  RST,
  input  EN,
  input  L_2,
  input  L_3,
  input  Input_1,
  output [3:0] key,
  output C,
  output C_1,
  output C_2,
  output C_3,
  output REQ
);

  wire dd_lhit, Keypad_FSM_1_we;
  wire [3:0] aaaa_k0;

  cltokey aaaa (
    .C3(C_3), .C2(C_2), .C1(C_1), .C0(C), .L3(L_3), .L2(L_2), .L1(L_1), .L0(L), .K3(aaaa_k0[3]),
    .K2(aaaa_k0[2]), .K1(aaaa_k0[1]), .K0(aaaa_k0[0]));
  Detect_ligne dd (.L({L_3, L_2, L_1, L}), .Lhit(dd_lhit));
  Keypad_FSM Keypad_FSM_1 (
    .clk(clk), .rst(RST), .en(EN), .lhit(dd_lhit), .ack(Input_1), .req(REQ), .WE(Keypad_FSM_1_we),
    .C({C_3, C_2, C_1, C}));
  Stockage bb (.Key(aaaa_k0), .WE(Keypad_FSM_1_we), .CLK(clk), .RST(RST), .Key_out(key));
endmodule

// qqqqqqq
module test_keypad (
);

  wire clk_out, fgfgf_sw1, fgfgf_sw2, fgfgf_sw3, KeyPad_1_p1, KeyPad_1_p2, KeyPad_1_p3, KeyPad_1_p4,
       KeyPad_1_p5, KeyPad_1_p6, KeyPad_1_p7, KeyPad_1_p8, L_7_Segment_Display_1_p1,
       L_7_Segment_Display_2_p1, test_keypad_decoder_1_req;
  wire [3:0] test_keypad_decoder_1_key;

  Clock sysclk ();  // open: out
  // KeyPad KeyPad_1: pin names not known; wires that end beside it: KeyPad_1_p1, KeyPad_1_p2, KeyPad_1_p3, KeyPad_1_p4, KeyPad_1_p5, KeyPad_1_p6, KeyPad_1_p7, KeyPad_1_p8
  DipSwitch #(.number(3)) fgfgf (.sw1(fgfgf_sw1), .sw2(fgfgf_sw2), .sw3(fgfgf_sw3));
  Clock clk (.out(clk_out));
  test_keypad_decoder test_keypad_decoder_1 (
    .clk(clk_out), .L(KeyPad_1_p5), .L_1(KeyPad_1_p6), .RST(fgfgf_sw1), .EN(fgfgf_sw2), .L_2(KeyPad_1_p7),
    .L_3(KeyPad_1_p8), .Input_1(fgfgf_sw3), .key(test_keypad_decoder_1_key), .C(KeyPad_1_p1),
    .C_1(KeyPad_1_p2), .C_2(KeyPad_1_p3), .C_3(KeyPad_1_p4), .REQ(test_keypad_decoder_1_req));
  LED fdgdfg (.in(test_keypad_decoder_1_req));
  // _7_Segment_Display L_7_Segment_Display_1: pin names not known; wires that end beside it: L_7_Segment_Display_1_p1, L_7_Segment_Display_1_p1
  // BCD_to_7_Segment_decoder bcd_to_7_segment_decoder_1: pin names not known
  // Binary_to_BCD_converter #(.binvalue(4)) binary_to_bcd_converter_1: pin names not known; wires that end beside it: test_keypad_decoder_1_key
  // BCD_to_7_Segment_decoder bcd_to_7_segment_decoder_2: pin names not known
  // _7_Segment_Display L_7_Segment_Display_2: pin names not known; wires that end beside it: L_7_Segment_Display_2_p1, L_7_Segment_Display_2_p1
endmodule
