// Logisim project TP78_SEN2.circ as structural Verilog: 12 circuits, main circuit UAL_calc
module UAL_calc (
  input  [1:0] Op,
  input  [15:0] In0,
  input  [15:0] In1,
  output [15:0] R
);

  wire [15:0] adder_1_out, adder_2_out, multiplexer_1_out, multiplier_1_out, subtractor_1_out;

  Multiplexer #(.width(16), .enable("false")) multiplexer_1 (
    .in0(In1), .in1(16'ha), .out(multiplexer_1_out), .sel(Op[0]));
  Adder #(.width(16)) adder_1 (.a(In0), .b(In1), .out(adder_1_out));  // open: cin, cout
  Subtractor #(.width(16)) subtractor_1 (.a(In1), .b(In0), .out(subtractor_1_out));  // open: bin, bout
  Multiplier #(.width(16)) multiplier_1 (.a(In0), .b(multiplexer_1_out), .out(multiplier_1_out));  // open: cin, cout
  Adder #(.width(16)) adder_2 (.a(multiplier_1_out), .b(In1), .out(adder_2_out));  // open: cin, cout
  Multiplexer #(.select(2), .width(16), .enable("false")) multiplexer_2 (
    .in0(adder_1_out), .in1(subtractor_1_out), .in2(multiplier_1_out), .in3(adder_2_out), .out(R), .sel(Op));
endmodule

module test_UAL_calc (
  input  [1:0] Op,
  input  [15:0] In0,
  input  [15:0] In1,
  output [15:0] R
);

  UAL_calc ual_calc_1 (.Op(Op), .In0(In0), .In1(In1), .R(R));
endmodule

module unite_de_calcul (
  input  WEA,
  input  WEB,
  input  WENxt,
  input  SELA,
  input  SELB,
  input  Selnxt,
  input  [1:0] OP,
  input  SELIn1,
  input  showA,
  input  showB,
  input  clk,
  input  rst,
  input  [3:0] key,
  output [3:0] out_14,
  output [1:0] out_15,
  output [15:0] out_16,
  output [15:0] out_17
);

  wire affiche_q, and_1_out, bcd_to_7_segment_decoder_2_p1, bcd_to_7_segment_decoder_3_p1,
       bcd_to_7_segment_decoder_4_p1, binary_to_bcd_converter_1_p2, isDigit, or_1_out;
  wire [3:0] multiplexer_1_out;
  wire [15:0] B_q, bit_extender_1_out, multiplexer_2_out, multiplexer_3_out, multiplexer_4_out, undriven;

  Multiplexer #(.width(4), .enable("false")) multiplexer_1 (
    .in0(key), .in1(4'b1111), .out(multiplexer_1_out), .sel(Selnxt));
  Comparator #(.width(4), .mode("unsigned")) comparator_1 (.a(4'b1010), .b(key), .gt(isDigit));  // open: eq, lt
  and and_1 (and_1_out, showA, ~showB);  // AND_Gate
  or or_1 (or_1_out, showA, showB);
  Register #(.width(4)) nxt_op (.D(multiplexer_1_out), .en(WENxt), .clk(clk), .Q(out_14), .clr(rst));
  Register #(.width(1)) affiche (.D(and_1_out), .en(or_1_out), .clk(clk), .Q(affiche_q), .clr(rst));
  Multiplexer #(.width(16), .enable("false")) multiplexer_2 (
    .in0(undriven), .in1({16{1'b0}}), .out(multiplexer_2_out), .sel(SELA));
  Multiplexer #(.width(16), .enable("false")) multiplexer_3 (
    .in0({16{1'b0}}), .in1(undriven), .out(multiplexer_3_out), .sel(SELB));
  Register #(.width(16)) A (.D(multiplexer_2_out), .en(WEA), .clk(clk), .Q(out_16), .clr(rst));
  Register #(.width(16)) B (.D(multiplexer_3_out), .en(WEB), .clk(clk), .Q(B_q), .clr(rst));
  Multiplexer #(.width(16), .enable("false")) multiplexer_4 (
    .in0(B_q), .in1(out_16), .out(multiplexer_4_out), .sel(affiche_q));
  assign bit_extender_1_out = {{12{1'b0}}, key};  // Bit_Extender bit_extender_1
  _7_Segment_Display Seg2 ();  // open: g, f, a, b, e, d, c, dp
  _7_Segment_Display Seg3 ();  // open: g, f, a, b, e, d, c, dp
  // BCD_to_7_Segment_decoder bcd_to_7_segment_decoder_1: pin names not known
  // BCD_to_7_Segment_decoder bcd_to_7_segment_decoder_2: pin names not known; wires that end beside it: bcd_to_7_segment_decoder_2_p1
  // Binary_to_BCD_converter #(.binvalue(12)) binary_to_bcd_converter_1: pin names not known; wires that end beside it: multiplexer_4_out[11:0], binary_to_bcd_converter_1_p2, binary_to_bcd_converter_1_p2, bcd_to_7_segment_decoder_2_p1, OP, out_16, out_17
  Multiplexer #(.width(16), .enable("false")) multiplexer_5 (
    .in0(B_q), .in1(bit_extender_1_out), .out(out_17), .sel(SELIn1));
  _7_Segment_Display Seg1 ();  // open: g, f, a, b, e, d, c, dp
  // BCD_to_7_Segment_decoder bcd_to_7_segment_decoder_3: pin names not known; wires that end beside it: bcd_to_7_segment_decoder_3_p1, bcd_to_7_segment_decoder_3_p1
  _7_Segment_Display Seg0 ();  // open: g, f, a, b, e, d, c, dp
  // BCD_to_7_Segment_decoder bcd_to_7_segment_decoder_4: pin names not known; wires that end beside it: bcd_to_7_segment_decoder_4_p1, bcd_to_7_segment_decoder_4_p1
  // Probe on undriven

  assign out_15 = OP;

  // Other names for the same wires on the sheet: nxt_op[3:0] = out_14

  // Notes on the sheet:
  //   Unit茅 de calcul
endmodule

module test_unite_de_calcul (
);

  unite_de_calcul unite_de_calcul_1 ();  // open: WEA, WEB, WENxt, SELA, SELB, Selnxt, OP, SELIn1, showA, showB, clk, rst, key, out_14, out_15, out_16, out_17
endmodule

module Keypad_FSM (
  input  clk,
  input  rst,
  input  en,
  input  lhit,
  input  ack,
  output req,
  output WE,
  output [3:0] C
);
endmodule

module cltokey (
  input  C3,
  input  C2,
  input  C1,
  input  C0,
  input  L3,
  input  L2,
  input  L1,
  input  L0,
  output K3,
  output K2,
  output K1,
  output K0
);

  wire and_1_out, and_2_out, and_3_out, and_4_out, and_5_out, and_6_out, and_7_out, and_8_out, and_9_out,
       and_10_out, and_11_out, not_1_out, not_2_out, not_3_out, not_4_out, not_5_out, not_6_out, not_7_out,
       not_8_out, not_9_out;

  not not_1 (not_1_out, C0);
  and and_1 (and_1_out, not_1_out, L2);
  not not_2 (not_2_out, C1);
  and and_2 (and_2_out, not_2_out, L3);
  and and_3 (and_3_out, C0, L2);
  not not_3 (not_3_out, C0);
  and and_4 (and_4_out, not_3_out, L0);
  not not_4 (not_4_out, L1);
  and and_5 (and_5_out, C0, not_4_out, not_5_out);
  not not_5 (not_5_out, L0);
  and and_6 (and_6_out, C2, not_6_out);
  not not_6 (not_6_out, L2);
  and and_7 (and_7_out, C3, L1);
  not not_7 (not_7_out, C1);
  and and_8 (and_8_out, not_7_out, L0);
  not not_8 (not_8_out, C1);
  and and_9 (and_9_out, not_8_out, L2);
  and and_10 (and_10_out, C1, L1);
  and and_11 (and_11_out, C2, not_9_out);
  not not_9 (not_9_out, L1);
  or or_1 (K3, and_1_out, and_2_out, C3);
  or or_2 (K2, L1, and_3_out, C3);
  or or_3 (K1, and_4_out, and_5_out, and_6_out, and_7_out);
  or or_4 (K0, and_8_out, and_9_out, and_10_out, and_11_out);
endmodule

module Stockage (
  input  [3:0] Key,
  input  WE,
  input  CLK,
  input  RST,
  output [3:0] Key_out
);

  Register #(.width(4)) register_1 (.D(Key), .en(WE), .clk(CLK), .Q(Key_out), .clr(RST));
endmodule

module Detect_ligne (
  input  [3:0] L,
  output Lhit
);

  or or_1 (Lhit, L[0], L[1], L[2], L[3]);
endmodule

module test_keypad_decoder (
  input  clk,
  input  L,
  input  L_1,
  input  RST,
  input  EN,
  input  L_2,
  input  L_3,
  input  Input_1,
  output [3:0] key,
  output C,
  output C_1,
  output C_2,
  output C_3,
  output REQ
);

  wire dd_lhit, Keypad_FSM_1_we;
  wire [3:0] aaaa_k0;

  cltokey aaaa (
    .C3(C_3), .C2(C_2), .C1(C_1), .C0(C), .L3(L_3), .L2(L_2), .L1(L_1), .L0(L), .K3(aaaa_k0[3]),
    .K2(aaaa_k0[2]), .K1(aaaa_k0[1]), .K0(aaaa_k0[0]));
  Detect_ligne dd (.L({L_3, L_2, L_1, L}), .Lhit(dd_lhit));
  Keypad_FSM Keypad_FSM_1 (
    .clk(clk), .rst(RST), .en(EN), .lhit(dd_lhit), .ack(Input_1), .req(REQ), .WE(Keypad_FSM_1_we),
    .C({C_3, C_2, C_1, C}));
  Stockage bb (.Key(aaaa_k0), .WE(Keypad_FSM_1_we), .CLK(clk), .RST(RST), .Key_out(key));
endmodule

// qqqqqqq
module test_keypad (
);

  wire aff0_p1, aff1_p1, clk_out, fgfgf_sw1, fgfgf_sw2, fgfgf_sw3, KeyPad_1_p1, KeyPad_1_p2, KeyPad_1_p3,
       KeyPad_1_p4, KeyPad_1_p5, KeyPad_1_p6, KeyPad_1_p7, KeyPad_1_p8, test_keypad_decoder_1_req;
  wire [3:0] test_keypad_decoder_1_key;

  Clock sysclk ();  // open: out
  // KeyPad KeyPad_1: pin names not known; wires that end beside it: KeyPad_1_p1, KeyPad_1_p2, KeyPad_1_p3, KeyPad_1_p4, KeyPad_1_p5, KeyPad_1_p6, KeyPad_1_p7, KeyPad_1_p8
  DipSwitch #(.number(3)) fgfgf (.sw1(fgfgf_sw1), .sw2(fgfgf_sw2), .sw3(fgfgf_sw3));
  Clock clk (.out(clk_out));
  test_keypad_decoder test_keypad_decoder_1 (
    .clk(clk_out), .L(KeyPad_1_p5), .L_1(KeyPad_1_p6), .RST(fgfgf_sw1), .EN(fgfgf_sw2), .L_2(KeyPad_1_p7),
    .L_3(KeyPad_1_p8), .Input_1(fgfgf_sw3), .key(test_keypad_decoder_1_key), .C(KeyPad_1_p1),
    .C_1(KeyPad_1_p2), .C_2(KeyPad_1_p3), .C_3(KeyPad_1_p4), .REQ(test_keypad_decoder_1_req));
  LED fdgdfg (.in(test_keypad_decoder_1_req));
  // BCD_to_7_Segment_decoder bcd_to_7_segment_decoder_1: pin names not known
  // _7_Segment_Display aff1: pin names not known; wires that end beside it: aff1_p1, aff1_p1, 1'b0
  // BCD_to_7_Segment_decoder bcd_to_7_segment_decoder_2: pin names not known
  // _7_Segment_Display aff0: pin names not known; wires that end beside it: aff0_p1, aff0_p1, 1'b0
  // Binary_to_BCD_converter #(.binvalue(4)) binary_to_bcd_converter_1: pin names not known; wires that end beside it: test_keypad_decoder_1_key
endmodule

module keypad_interface (
  input  clk,
  input  [3:0] L,
  input  rst,
  input  ACK,
  output [3:0] key,
  output [3:0] C,
  output REQ
);

  // FSM_Entity #(.content("state_machine interface_FSM_1 @[419,69,1000,750]{\n	in REQ[1]   @[419,324,32,15];\n	out ACK[1]   @[1389,433,30,15];\n	codeWidth = 3;\n	reset = S0;\n	\n	state S0[\"000\"]:\n	 	@[713,265,30,30]\n		set ACK=\"0\";  @[713,265,30,30]	\n		goto S1  when REQ   @[843,235,32,22]; \n	state S1[\"001\"]:\n	 	@[923,269,30,30]\n		set ACK=\"1\";  @[923,269,30,30]	\n		goto S0  when (REQ==\"0\")   @[826,336,69,22]; \n}")) numpad_interface: pin names not known; wires that end beside it: clk, rst, 1'b1, REQ, ACK
  test_keypad_decoder numpad_decoder (
    .clk(clk), .L(L[0]), .L_1(L[1]), .RST(rst), .EN(1'b1), .L_2(L[2]), .L_3(L[3]), .Input_1(ACK), .key(key),
    .C(C[0]), .C_1(C[1]), .C_2(C[2]), .C_3(C[3]), .REQ(REQ));
endmodule

module calculatrice (
  input  rst
);

  wire ACK, affiche_q, and_1_out, bcd_to_7_segment_decoder_2_p12, bcd_to_7_segment_decoder_3_p1,
       bcd_to_7_segment_decoder_4_p1, binary_to_bcd_converter_1_p2, clk, isDigit, or_1_out, REQ, SelA, SelB,
       SelIn1, Selnxt, showA, showB, WEA, WEB, WENxt;
  wire [1:0] Op;
  wire [3:0] key, KeyPad_1_p1, KeyPad_1_p5, multiplexer_1_out, nxt_op;
  wire [15:0] A_q, B_q, bit_extender_1_out, multiplexer_2_out, multiplexer_3_out, multiplexer_4_out,
       multiplexer_5_out, ual_calc_1_r;

  // KeyPad KeyPad_1: pin names not known; wires that end beside it: KeyPad_1_p1[0], KeyPad_1_p1[1], KeyPad_1_p1[2], KeyPad_1_p1[3], KeyPad_1_p5[0], KeyPad_1_p5[1], KeyPad_1_p5[2], KeyPad_1_p5[3]
  Clock u_clk (.out(clk));
  // Probe on key
  // Probe on nxt_op
  Multiplexer #(.width(4), .enable("false")) multiplexer_1 (
    .in0(key), .in1(4'b1111), .out(multiplexer_1_out), .sel(Selnxt));
  Comparator #(.width(4), .mode("unsigned")) comparator_1 (.a(4'b1010), .b(key), .gt(isDigit));  // open: eq, lt
  keypad_interface keypad_interface_1 (
    .clk(clk), .L(KeyPad_1_p5), .rst(rst), .ACK(ACK), .key(key), .C(KeyPad_1_p1), .REQ(REQ));
  and and_1 (and_1_out, showA, ~showB);  // AND_Gate
  or or_1 (or_1_out, showA, showB);
  Register #(.width(4)) u_nxt_op (.D(multiplexer_1_out), .en(WENxt), .clk(clk), .Q(nxt_op), .clr(rst));
  Register #(.width(1)) affiche (.D(and_1_out), .en(or_1_out), .clk(clk), .Q(affiche_q), .clr(rst));
  _7_Segment_Display hex_key ();  // open: g, f, a, b, e, d, c, dp
  // Bin_to_7_Segment_decoder bin_to_7_segment_decoder_1: pin names not known; wires that end beside it: key
  Multiplexer #(.width(16), .enable("false")) multiplexer_2 (
    .in0(ual_calc_1_r), .in1({16{1'b0}}), .out(multiplexer_2_out), .sel(SelA));
  Multiplexer #(.width(16), .enable("false")) multiplexer_3 (
    .in0({16{1'b0}}), .in1(ual_calc_1_r), .out(multiplexer_3_out), .sel(SelB));
  Register #(.width(16)) A (.D(multiplexer_2_out), .en(WEA), .clk(clk), .Q(A_q), .clr(rst));
  Register #(.width(16)) B (.D(multiplexer_3_out), .en(WEB), .clk(clk), .Q(B_q), .clr(rst));
  Multiplexer #(.width(16), .enable("false")) multiplexer_4 (
    .in0(B_q), .in1(A_q), .out(multiplexer_4_out), .sel(affiche_q));
  assign bit_extender_1_out = {{12{1'b0}}, key};  // Bit_Extender bit_extender_1
  // BCD_to_7_Segment_decoder bcd_to_7_segment_decoder_1: pin names not known; wires that end beside it: 1'b1, REQ, key, isDigit, nxt_op
  _7_Segment_Display Seg2 ();  // open: g, f, a, b, e, d, c, dp
  _7_Segment_Display Seg3 ();  // open: g, f, a, b, e, d, c, dp
  // BCD_to_7_Segment_decoder bcd_to_7_segment_decoder_2: pin names not known; wires that end beside it: ACK, showA, showB, SelIn1, WEA, WEB, SelB, SelA, Op, WENxt, Selnxt, bcd_to_7_segment_decoder_2_p12
  // Binary_to_BCD_converter #(.binvalue(12)) binary_to_bcd_converter_1: pin names not known; wires that end beside it: multiplexer_4_out[11:0], binary_to_bcd_converter_1_p2, binary_to_bcd_converter_1_p2, bcd_to_7_segment_decoder_2_p12
  // Probe on Op
  // Probe on multiplexer_5_out
  Multiplexer #(.width(16), .enable("false")) multiplexer_5 (
    .in0(B_q), .in1(bit_extender_1_out), .out(multiplexer_5_out), .sel(SelIn1));
  // BCD_to_7_Segment_decoder bcd_to_7_segment_decoder_3: pin names not known; wires that end beside it: bcd_to_7_segment_decoder_3_p1, bcd_to_7_segment_decoder_3_p1
  _7_Segment_Display Seg1 ();  // open: g, f, a, b, e, d, c, dp
  // BCD_to_7_Segment_decoder bcd_to_7_segment_decoder_4: pin names not known; wires that end beside it: bcd_to_7_segment_decoder_4_p1, bcd_to_7_segment_decoder_4_p1
  _7_Segment_Display Seg0 ();  // open: g, f, a, b, e, d, c, dp
  // Probe on ual_calc_1_r
  UAL_calc ual_calc_1 (.Op(Op), .In0(A_q), .In1(multiplexer_5_out), .R(ual_calc_1_r));

  // Notes on the sheet:
  //   Interface Keypad
  //   Unit茅 de calcul
  //   Unit茅 de contr么le
  //   UAL_calc
endmodule
