// Logisim project Tpexamen.circ as structural Verilog: 2 circuits, main circuit main
module main (
  input  rst,
  input  clk,
  input  EN,
  input  [2:0] in_4,
  output L1,
  output L2,
  output L3,
  output L4,
  output L5
);

  wire ruban_p5;
  wire [4:0] ruban_p7, ruban_p8;

  // FSM_Entity #(.content("state_machine examen @[50,50,800,500]{\n	in A[3]   @[50,100,36,15];\n	out WE[5]   @[802,263,48,15];D[5]   @[813,437,37,15];\n	codeWidth = 4;\n	reset = S0;\n	\n	state S0[\"0000\"]:\n	 	@[128,147,30,30]\n		set WE=\"00000\";D=\"00000\";  @[128,147,30,30]	\n		goto S1  when default   @[232,176,40,24]; \n	state S1[\"0001\"]:\n	 	@[304,190,30,30]\n		set WE=\"00001\";D=\"00001\";  @[304,190,30,30]	\n		goto S2  when default   @[378,189,40,24]; \n	state S2[\"0010\"]:\n	 	@[424,185,30,30]\n		set WE=\"00010\";D=\"00010\";  @[424,185,30,30]	\n		goto S3  when default   @[513,181,40,24]; \n	state S3[\"0011\"]:\n	 	@[572,154,30,30]\n		set WE=\"00100\";D=\"00100\";  @[572,154,30,30]	\n		goto S4  when default   @[619,210,40,24]; \n	state S4[\"0100\"]:\n	 	@[652,244,30,30]\n		set WE=\"01000\";D=\"01000\";  @[652,244,30,30]	\n		goto S5  when default   @[606,313,40,24]; \n	state S5[\"0101\"]:\n	 	@[611,347,30,30]\n		set WE=\"10000\";D=\"10000\";  @[611,347,30,30]	\n		goto S6  when default   @[544,386,40,24]; \n	state S6[\"0110\"]:\n	 	@[500,448,30,30]\n		set WE=\"00001\";D=\"00000\";  @[500,448,30,30]	\n		goto S7  when default   @[437,440,40,24]; \n	state S7[\"0111\"]:\n	 	@[360,466,30,30]\n		set WE=\"00010\";D=\"00000\";  @[360,466,30,30]	\n		goto S8  when default   @[293,467,40,24]; \n	state S8[\"1000\"]:\n	 	@[228,457,30,30]\n		set WE=\"00100\";D=\"00000\";  @[228,457,30,30]	\n		goto S9  when default   @[185,439,40,24]; \n	state S9[\"1001\"]:\n	 	@[105,405,30,30]\n		set WE=\"01000\";D=\"00000\";  @[105,405,30,30]	\n		goto S10  when default   @[102,359,40,24]; \n	state S10[\"1010\"]:\n	 	@[74,279,30,30]\n		set WE=\"10000\";D=\"00000\";  @[74,279,30,30]	\n		goto S0  when default   @[112,230,40,24]; \n}")) ruban: pin names not known; wires that end beside it: clk, rst, EN, in_4, ruban_p5, ruban_p5, ruban_p7, ruban_p8
  Register #(.width(1)) register_1 (.D(ruban_p8[0]), .en(ruban_p7[0]), .clk(clk), .Q(L1), .clr(rst));
  Register #(.width(1)) register_2 (.D(ruban_p8[1]), .en(ruban_p7[1]), .clk(clk), .Q(L2), .clr(rst));
  Register #(.width(1)) register_3 (.D(ruban_p8[2]), .en(ruban_p7[2]), .clk(clk), .Q(L3), .clr(rst));
  Register #(.width(1)) register_4 (.D(ruban_p8[3]), .en(ruban_p7[3]), .clk(clk), .Q(L4), .clr(rst));
  Register #(.width(1)) register_5 (.D(ruban_p8[4]), .en(ruban_p7[4]), .clk(clk), .Q(L5), .clr(rst));
endmodule

module TEST (
  input  in_1,
  input  in_2
);

  wire clock_1_out, main_1_l1, main_1_l2, main_1_l3, main_1_l4, main_1_l5;

  Clock sysclk ();  // open: out
  Clock clock_1 (.out(clock_1_out));
  LED led_1 (.in(main_1_l1));
  main main_1 (
    .rst(in_1), .clk(clock_1_out), .EN(in_2), .L1(main_1_l1), .L2(main_1_l2), .L3(main_1_l3), .L4(main_1_l4),
    .L5(main_1_l5));  // open: in_4
  LED led_2 (.in(main_1_l2));
  LED led_3 (.in(main_1_l3));
  LED led_4 (.in(main_1_l4));
  LED led_5 (.in(main_1_l5));
endmodule
